// Logisim project Tetris.circ as structural Verilog: 64 circuits, main circuit main
module main (
  input  DS0,
  input  DS1,
  input  DS2,
  input  DS3,
  input  DS4,
  input  DS5,
  input  DS6,
  input  DS7
);

  wire ButtonLeft, ButtonRight, Clock, GameReset, LED_Connector_1_output_1, LED_Connector_1_output_2,
       LED_Connector_1_output_3, LED_Connector_1_output_4, LED_Connector_1_output_5,
       LED_Connector_1_output_6, LED_Connector_1_output_7, LED_Connector_1_output_8,
       LED_Connector_2_output_1, LED_Connector_2_output_2, LED_Connector_2_output_3,
       LED_Connector_2_output_4, LED_Connector_2_output_5, LED_Connector_2_output_6,
       LED_Connector_2_output_7, LED_Connector_2_output_8, LED_Connector_3_output_1,
       LED_Connector_3_output_2, LED_Connector_3_output_3, LED_Connector_3_output_4,
       LED_Connector_3_output_5, LED_Connector_3_output_6, LED_Connector_3_output_7,
       LED_Connector_3_output_8, LED_Connector_4_output_1, LED_Connector_4_output_2,
       LED_Connector_4_output_3, LED_Connector_4_output_4, LED_Connector_4_output_5,
       LED_Connector_4_output_6, LED_Connector_4_output_7, LED_Connector_4_output_8,
       LED_Connector_5_output_1, LED_Connector_5_output_2, LED_Connector_5_output_3,
       LED_Connector_5_output_4, LED_Connector_5_output_5, LED_Connector_5_output_6,
       LED_Connector_5_output_7, LED_Connector_5_output_8, LED_Connector_6_output_1,
       LED_Connector_6_output_2, LED_Connector_6_output_3, LED_Connector_6_output_4,
       LED_Connector_6_output_5, LED_Connector_6_output_6, LED_Connector_6_output_7,
       LED_Connector_6_output_8, LED_Connector_7_output_1, LED_Connector_7_output_2,
       LED_Connector_7_output_3, LED_Connector_7_output_4, LED_Connector_7_output_5,
       LED_Connector_7_output_6, LED_Connector_7_output_7, LED_Connector_7_output_8,
       LED_Connector_8_output_1, LED_Connector_8_output_2, LED_Connector_8_output_3,
       LED_Connector_8_output_4, LED_Connector_8_output_5, LED_Connector_8_output_6,
       LED_Connector_8_output_7, LED_Connector_8_output_8, LED_Connector_9_output_1,
       LED_Connector_9_output_2, LED_Connector_9_output_3, LED_Connector_9_output_4,
       LED_Connector_9_output_5, LED_Connector_9_output_6, LED_Connector_9_output_7,
       LED_Connector_9_output_8, LED_Connector_10_output_1, LED_Connector_10_output_2,
       LED_Connector_10_output_3, LED_Connector_10_output_4, LED_Connector_10_output_5,
       LED_Connector_10_output_6, LED_Connector_10_output_7, LED_Connector_10_output_8,
       LED_Connector_11_output_1, LED_Connector_11_output_2, LED_Connector_11_output_3,
       LED_Connector_11_output_4, LED_Connector_11_output_5, LED_Connector_11_output_6,
       LED_Connector_11_output_7, LED_Connector_11_output_8, LED_Connector_12_output_1,
       LED_Connector_12_output_2, LED_Connector_12_output_3, LED_Connector_12_output_4,
       LED_Connector_12_output_5, LED_Connector_12_output_6, LED_Connector_12_output_7,
       LED_Connector_12_output_8, LineBlink, LineShift, not_1_out, or_1_out, PlayerReset, ResetButton_out,
       WriteEnable;
  wire [1:0] BlockWriteState_1_output_bus_1, CurrentState, GameOverState_1_output_bus_4,
       MUX4x2_1_output_bus_1, player_fsm_1_next_state2, ScorePointState_1_output_bus_1;
  wire [3:0] BlockWriteState_1_output_bus_3, line, player_fsm_1_read_line, raddr, waddr;
  wire [7:0] DisplayDriver_1_output_bus_1, DisplayDriver_1_output_bus_2, DisplayDriver_1_output_bus_3,
       DisplayDriver_1_output_bus_4, DisplayDriver_1_output_bus_6, DisplayDriver_1_output_bus_7,
       DisplayDriver_1_output_bus_8, DisplayDriver_1_output_bus_9, DisplayDriver_1_output_bus_10,
       DisplayDriver_1_output_bus_11, DisplayDriver_1_output_bus_12, DisplayDriver_1_output_bus_13,
       DrawPlayer_1_output_bus_1, DrawPlayer_1_output_bus_2, DrawPlayer_1_output_bus_3,
       DrawPlayer_1_output_bus_4, DrawPlayer_1_output_bus_5, DrawPlayer_1_output_bus_6,
       DrawPlayer_1_output_bus_7, DrawPlayer_1_output_bus_8, DrawPlayer_1_output_bus_9,
       DrawPlayer_1_output_bus_10, DrawPlayer_1_output_bus_11, DrawPlayer_1_output_bus_12,
       GameOverState_1_output_bus_1, GameOverState_1_output_bus_2, GameOverState_1_output_bus_3,
       GameOverState_1_output_bus_5, GameOverState_1_output_bus_6, GameOverState_1_output_bus_7,
       GameOverState_1_output_bus_8, GameOverState_1_output_bus_9, GameOverState_1_output_bus_10,
       GameOverState_1_output_bus_11, GameOverState_1_output_bus_12, GameOverState_1_output_bus_13,
       Mask8bit_1_output_bus_1, player, rdata, score, wdata;

  Clock clock_1 (.out(Clock));
  // Probe on CurrentState
  // Probe on score
  // Probe on player
  // Probe on line
  DisplayDriver DisplayDriver_1 (
    .Input_bus_3(wdata), .Input_bus_2(waddr), .Input_bus_1(raddr), .Input_4(LineShift), .Input_2(Clock),
    .Input_3(WriteEnable), .Input_1(GameReset), .Output_bus_3(DisplayDriver_1_output_bus_3),
    .Output_bus_4(DisplayDriver_1_output_bus_4), .Output_bus_11(DisplayDriver_1_output_bus_11),
    .Output_bus_13(DisplayDriver_1_output_bus_13), .Output_bus_12(DisplayDriver_1_output_bus_12),
    .Output_bus_2(DisplayDriver_1_output_bus_2), .Output_bus_6(DisplayDriver_1_output_bus_6),
    .Output_bus_9(DisplayDriver_1_output_bus_9), .Output_bus_1(DisplayDriver_1_output_bus_1),
    .Output_bus_7(DisplayDriver_1_output_bus_7), .Output_bus_8(DisplayDriver_1_output_bus_8),
    .Output_bus_10(DisplayDriver_1_output_bus_10), .Output_bus_5(rdata));
  Button ResetButton (.out(ResetButton_out));
  or or_1 (or_1_out, GameReset, ResetButton_out, PlayerReset);
  DrawPlayer DrawPlayer_1 (
    .Player(player), .ShowPlayer(1'b1), .PlayerLine(line), .Input_bus_11(DisplayDriver_1_output_bus_3),
    .Input_bus_8(DisplayDriver_1_output_bus_4), .Input_bus_9(DisplayDriver_1_output_bus_11),
    .Input_bus_6(DisplayDriver_1_output_bus_13), .Input_bus_1(DisplayDriver_1_output_bus_12),
    .Input_bus_12(DisplayDriver_1_output_bus_2), .Input_bus_2(DisplayDriver_1_output_bus_6),
    .Input_bus_3(DisplayDriver_1_output_bus_9), .Input_bus_4(DisplayDriver_1_output_bus_1),
    .Input_bus_5(DisplayDriver_1_output_bus_7), .Input_bus_7(DisplayDriver_1_output_bus_8),
    .Input_bus_10(DisplayDriver_1_output_bus_10), .Output_bus_1(DrawPlayer_1_output_bus_1),
    .Output_bus_3(DrawPlayer_1_output_bus_3), .Output_bus_2(DrawPlayer_1_output_bus_2),
    .Output_bus_5(DrawPlayer_1_output_bus_5), .Output_bus_10(DrawPlayer_1_output_bus_10),
    .Output_bus_7(DrawPlayer_1_output_bus_7), .Output_bus_4(DrawPlayer_1_output_bus_4),
    .Output_bus_9(DrawPlayer_1_output_bus_9), .Output_bus_11(DrawPlayer_1_output_bus_11),
    .Output_bus_8(DrawPlayer_1_output_bus_8), .Output_bus_6(DrawPlayer_1_output_bus_6),
    .Output_bus_12(DrawPlayer_1_output_bus_12));
  Mask8bit Mask8bit_1 (
    .Input_bus_1(DrawPlayer_1_output_bus_12), .Input_1(not_1_out), .Output_bus_1(Mask8bit_1_output_bus_1));
  not not_1 (not_1_out, LineBlink);
  player_fsm player_fsm_1 (
    .right_button(ButtonRight), .left_button(ButtonLeft), .nb_side({2'b00, DS5, DS4}), .data_line(rdata),
    .current_state2(CurrentState), .reset(or_1_out), .clock(Clock), .player2(player),
    .read_line(player_fsm_1_read_line), .player_line(line), .next_state2(player_fsm_1_next_state2));
  BlockWriteState BlockWriteState_1 (
    .Input_bus_2(CurrentState), .Input_1(Clock), .Input_bus_1(line), .Player(player),
    .Output_bus_1(BlockWriteState_1_output_bus_1), .Output_1(WriteEnable), .Output_bus_2(waddr),
    .Output_bus_3(BlockWriteState_1_output_bus_3), .WriteData(wdata), .ReadLine(rdata));
  ScorePointState ScorePointState_1 (
    .Input_bus_1(CurrentState), .Output_bus_1(ScorePointState_1_output_bus_1), .Output_1(LineBlink),
    .Output_2(LineShift), .Input_1(Clock), .ScoreReset(GameReset), .Score(score), .clock_div({DS3, DS2}));
  GameOverState GameOverState_1 (
    .Input_bus_14(CurrentState), .Input_1(ButtonLeft), .Input_2(ButtonRight), .Input_bus_1(score),
    .Input_bus_9(DrawPlayer_1_output_bus_1), .Input_bus_5(DrawPlayer_1_output_bus_3),
    .Input_bus_2(DrawPlayer_1_output_bus_2), .Input_bus_10(DrawPlayer_1_output_bus_5),
    .Input_bus_12(DrawPlayer_1_output_bus_10), .Input_bus_11(DrawPlayer_1_output_bus_7),
    .Input_bus_3(DrawPlayer_1_output_bus_4), .Input_bus_4(DrawPlayer_1_output_bus_9),
    .Input_bus_6(DrawPlayer_1_output_bus_11), .Input_bus_8(DrawPlayer_1_output_bus_8),
    .Input_bus_13(DrawPlayer_1_output_bus_6), .Input_bus_7(Mask8bit_1_output_bus_1),
    .Output_bus_4(GameOverState_1_output_bus_4), .Output_1(GameReset),
    .Output_bus_3(GameOverState_1_output_bus_3), .Output_bus_9(GameOverState_1_output_bus_9),
    .Output_bus_11(GameOverState_1_output_bus_11), .Output_bus_5(GameOverState_1_output_bus_5),
    .Output_bus_8(GameOverState_1_output_bus_8), .Output_bus_13(GameOverState_1_output_bus_13),
    .Output_bus_6(GameOverState_1_output_bus_6), .Output_bus_10(GameOverState_1_output_bus_10),
    .Output_bus_12(GameOverState_1_output_bus_12), .Output_bus_1(GameOverState_1_output_bus_1),
    .Output_bus_2(GameOverState_1_output_bus_2), .Output_bus_7(GameOverState_1_output_bus_7), .Clock(Clock));
  // Probe on MUX4x2_1_output_bus_1
  MUX4x2 MUX4x2_1 (
    .Input_bus_4(player_fsm_1_next_state2), .Input_bus_2(BlockWriteState_1_output_bus_1),
    .Input_bus_5(ScorePointState_1_output_bus_1), .Input_bus_1(GameOverState_1_output_bus_4),
    .Input_bus_3(CurrentState), .Output_bus_1(MUX4x2_1_output_bus_1));
  Register #(.width(2)) THE_STATE (.D(MUX4x2_1_output_bus_1), .en(1'b1), .clk(Clock), .Q(CurrentState), .clr(1'b0));
  LED L60 (.in(LED_Connector_12_output_1));
  LED L70 (.in(LED_Connector_12_output_7));
  LED_Connector LED_Connector_12 (
    .Input_bus_1(GameOverState_1_output_bus_3), .Output_7(LED_Connector_12_output_7),
    .Output_1(LED_Connector_12_output_1), .Output_5(LED_Connector_12_output_5),
    .Output_6(LED_Connector_12_output_6), .Output_3(LED_Connector_12_output_3),
    .Output_4(LED_Connector_12_output_4), .Output_8(LED_Connector_12_output_8),
    .Output_2(LED_Connector_12_output_2));
  LED L71 (.in(LED_Connector_9_output_7));
  LED L61 (.in(LED_Connector_9_output_1));
  LED_Connector LED_Connector_9 (
    .Input_bus_1(GameOverState_1_output_bus_9), .Output_7(LED_Connector_9_output_7),
    .Output_1(LED_Connector_9_output_1), .Output_5(LED_Connector_9_output_5),
    .Output_6(LED_Connector_9_output_6), .Output_3(LED_Connector_9_output_3),
    .Output_4(LED_Connector_9_output_4), .Output_8(LED_Connector_9_output_8),
    .Output_2(LED_Connector_9_output_2));
  LED_Connector LED_Connector_2 (
    .Input_bus_1(GameOverState_1_output_bus_11), .Output_7(LED_Connector_2_output_7),
    .Output_1(LED_Connector_2_output_1), .Output_5(LED_Connector_2_output_5),
    .Output_6(LED_Connector_2_output_6), .Output_3(LED_Connector_2_output_3),
    .Output_4(LED_Connector_2_output_4), .Output_8(LED_Connector_2_output_8),
    .Output_2(LED_Connector_2_output_2));
  LED L62 (.in(LED_Connector_2_output_1));
  LED L72 (.in(LED_Connector_2_output_7));
  LED L73 (.in(LED_Connector_6_output_7));
  LED_Connector LED_Connector_6 (
    .Input_bus_1(GameOverState_1_output_bus_5), .Output_7(LED_Connector_6_output_7),
    .Output_1(LED_Connector_6_output_1), .Output_5(LED_Connector_6_output_5),
    .Output_6(LED_Connector_6_output_6), .Output_3(LED_Connector_6_output_3),
    .Output_4(LED_Connector_6_output_4), .Output_8(LED_Connector_6_output_8),
    .Output_2(LED_Connector_6_output_2));
  LED L63 (.in(LED_Connector_6_output_1));
  LED L74 (.in(LED_Connector_4_output_7));
  LED_Connector LED_Connector_4 (
    .Input_bus_1(GameOverState_1_output_bus_8), .Output_7(LED_Connector_4_output_7),
    .Output_1(LED_Connector_4_output_1), .Output_5(LED_Connector_4_output_5),
    .Output_6(LED_Connector_4_output_6), .Output_3(LED_Connector_4_output_3),
    .Output_4(LED_Connector_4_output_4), .Output_8(LED_Connector_4_output_8),
    .Output_2(LED_Connector_4_output_2));
  LED L64 (.in(LED_Connector_4_output_1));
  LED L65 (.in(LED_Connector_11_output_1));
  LED L75 (.in(LED_Connector_11_output_7));
  LED_Connector LED_Connector_11 (
    .Input_bus_1(GameOverState_1_output_bus_13), .Output_7(LED_Connector_11_output_7),
    .Output_1(LED_Connector_11_output_1), .Output_5(LED_Connector_11_output_5),
    .Output_6(LED_Connector_11_output_6), .Output_3(LED_Connector_11_output_3),
    .Output_4(LED_Connector_11_output_4), .Output_8(LED_Connector_11_output_8),
    .Output_2(LED_Connector_11_output_2));
  LED_Connector LED_Connector_3 (
    .Input_bus_1(GameOverState_1_output_bus_6), .Output_7(LED_Connector_3_output_7),
    .Output_1(LED_Connector_3_output_1), .Output_5(LED_Connector_3_output_5),
    .Output_6(LED_Connector_3_output_6), .Output_3(LED_Connector_3_output_3),
    .Output_4(LED_Connector_3_output_4), .Output_8(LED_Connector_3_output_8),
    .Output_2(LED_Connector_3_output_2));
  LED L66 (.in(LED_Connector_3_output_1));
  LED L76 (.in(LED_Connector_3_output_7));
  LED L67 (.in(LED_Connector_5_output_1));
  LED_Connector LED_Connector_5 (
    .Input_bus_1(GameOverState_1_output_bus_10), .Output_7(LED_Connector_5_output_7),
    .Output_1(LED_Connector_5_output_1), .Output_5(LED_Connector_5_output_5),
    .Output_6(LED_Connector_5_output_6), .Output_3(LED_Connector_5_output_3),
    .Output_4(LED_Connector_5_output_4), .Output_8(LED_Connector_5_output_8),
    .Output_2(LED_Connector_5_output_2));
  LED L77 (.in(LED_Connector_5_output_7));
  LED L68 (.in(LED_Connector_8_output_1));
  LED L78 (.in(LED_Connector_8_output_7));
  LED_Connector LED_Connector_8 (
    .Input_bus_1(GameOverState_1_output_bus_12), .Output_7(LED_Connector_8_output_7),
    .Output_1(LED_Connector_8_output_1), .Output_5(LED_Connector_8_output_5),
    .Output_6(LED_Connector_8_output_6), .Output_3(LED_Connector_8_output_3),
    .Output_4(LED_Connector_8_output_4), .Output_8(LED_Connector_8_output_8),
    .Output_2(LED_Connector_8_output_2));
  LED L69 (.in(LED_Connector_10_output_1));
  LED L79 (.in(LED_Connector_10_output_7));
  LED_Connector LED_Connector_10 (
    .Input_bus_1(GameOverState_1_output_bus_1), .Output_7(LED_Connector_10_output_7),
    .Output_1(LED_Connector_10_output_1), .Output_5(LED_Connector_10_output_5),
    .Output_6(LED_Connector_10_output_6), .Output_3(LED_Connector_10_output_3),
    .Output_4(LED_Connector_10_output_4), .Output_8(LED_Connector_10_output_8),
    .Output_2(LED_Connector_10_output_2));
  LED L7A (.in(LED_Connector_1_output_7));
  LED_Connector LED_Connector_1 (
    .Input_bus_1(GameOverState_1_output_bus_2), .Output_7(LED_Connector_1_output_7),
    .Output_1(LED_Connector_1_output_1), .Output_5(LED_Connector_1_output_5),
    .Output_6(LED_Connector_1_output_6), .Output_3(LED_Connector_1_output_3),
    .Output_4(LED_Connector_1_output_4), .Output_8(LED_Connector_1_output_8),
    .Output_2(LED_Connector_1_output_2));
  LED L6A (.in(LED_Connector_1_output_1));
  LED L6B (.in(LED_Connector_7_output_1));
  LED L7B (.in(LED_Connector_7_output_7));
  LED_Connector LED_Connector_7 (
    .Input_bus_1(GameOverState_1_output_bus_7), .Output_7(LED_Connector_7_output_7),
    .Output_1(LED_Connector_7_output_1), .Output_5(LED_Connector_7_output_5),
    .Output_6(LED_Connector_7_output_6), .Output_3(LED_Connector_7_output_3),
    .Output_4(LED_Connector_7_output_4), .Output_8(LED_Connector_7_output_8),
    .Output_2(LED_Connector_7_output_2));
  MUX4x4 MUX4x4_1 (
    .Input_bus_1(player_fsm_1_read_line), .Input_bus_2(BlockWriteState_1_output_bus_3),
    .Input_bus_4(4'b0000), .Input_bus_5(4'b0000), .Input_bus_3(CurrentState), .Output_bus_1(raddr));
  LED L30 (.in(LED_Connector_12_output_3));
  LED L40 (.in(LED_Connector_12_output_6));
  LED L20 (.in(LED_Connector_12_output_4));
  LED L50 (.in(LED_Connector_12_output_5));
  LED L31 (.in(LED_Connector_9_output_3));
  LED L51 (.in(LED_Connector_9_output_5));
  LED L41 (.in(LED_Connector_9_output_6));
  LED L21 (.in(LED_Connector_9_output_4));
  LED L22 (.in(LED_Connector_2_output_4));
  LED L32 (.in(LED_Connector_2_output_3));
  LED L52 (.in(LED_Connector_2_output_5));
  LED L42 (.in(LED_Connector_2_output_6));
  LED L43 (.in(LED_Connector_6_output_6));
  LED L23 (.in(LED_Connector_6_output_4));
  LED L33 (.in(LED_Connector_6_output_3));
  LED L53 (.in(LED_Connector_6_output_5));
  LED L34 (.in(LED_Connector_4_output_3));
  LED L44 (.in(LED_Connector_4_output_6));
  LED L54 (.in(LED_Connector_4_output_5));
  LED L24 (.in(LED_Connector_4_output_4));
  LED L35 (.in(LED_Connector_11_output_3));
  LED L45 (.in(LED_Connector_11_output_6));
  LED L25 (.in(LED_Connector_11_output_4));
  LED L55 (.in(LED_Connector_11_output_5));
  LED L56 (.in(LED_Connector_3_output_5));
  LED L46 (.in(LED_Connector_3_output_6));
  LED L36 (.in(LED_Connector_3_output_3));
  LED L26 (.in(LED_Connector_3_output_4));
  LED L37 (.in(LED_Connector_5_output_3));
  LED L27 (.in(LED_Connector_5_output_4));
  LED L57 (.in(LED_Connector_5_output_5));
  LED L47 (.in(LED_Connector_5_output_6));
  LED L48 (.in(LED_Connector_8_output_6));
  LED L38 (.in(LED_Connector_8_output_3));
  LED L28 (.in(LED_Connector_8_output_4));
  LED L58 (.in(LED_Connector_8_output_5));
  LED L59 (.in(LED_Connector_10_output_5));
  LED L39 (.in(LED_Connector_10_output_3));
  LED L49 (.in(LED_Connector_10_output_6));
  LED L29 (.in(LED_Connector_10_output_4));
  LED L3A (.in(LED_Connector_1_output_3));
  LED L5A (.in(LED_Connector_1_output_5));
  LED L2A (.in(LED_Connector_1_output_4));
  LED L4A (.in(LED_Connector_1_output_6));
  LED L5B (.in(LED_Connector_7_output_5));
  LED L2B (.in(LED_Connector_7_output_4));
  LED L3B (.in(LED_Connector_7_output_3));
  LED L4B (.in(LED_Connector_7_output_6));
  Button Button_1 (.out(ButtonRight));
  Button Button_2 (.out(ButtonLeft));
  D_Flip_Flop d_ff_1 (.D(WriteEnable), .clk(Clock), .Q(PlayerReset), .reset(GameReset));  // open: Qn, preset
  LED L00 (.in(LED_Connector_12_output_2));
  LED L10 (.in(LED_Connector_12_output_8));
  LED L01 (.in(LED_Connector_9_output_2));
  LED L11 (.in(LED_Connector_9_output_8));
  LED L12 (.in(LED_Connector_2_output_8));
  LED L02 (.in(LED_Connector_2_output_2));
  LED L13 (.in(LED_Connector_6_output_8));
  LED L03 (.in(LED_Connector_6_output_2));
  LED L14 (.in(LED_Connector_4_output_8));
  LED L04 (.in(LED_Connector_4_output_2));
  LED L05 (.in(LED_Connector_11_output_2));
  LED L15 (.in(LED_Connector_11_output_8));
  LED L06 (.in(LED_Connector_3_output_2));
  LED L16 (.in(LED_Connector_3_output_8));
  LED L07 (.in(LED_Connector_5_output_2));
  LED L17 (.in(LED_Connector_5_output_8));
  LED L18 (.in(LED_Connector_8_output_8));
  LED L08 (.in(LED_Connector_8_output_2));
  LED L09 (.in(LED_Connector_10_output_2));
  LED L19 (.in(LED_Connector_10_output_8));
  LED L1A (.in(LED_Connector_1_output_8));
  LED L0A (.in(LED_Connector_1_output_2));
  LED L1B (.in(LED_Connector_7_output_8));
  LED L0B (.in(LED_Connector_7_output_2));

  // Notes on the sheet:
  //   DipSwitch
endmodule

module PlayerState (
  input  [1:0] Input_bus_1,
  input  [7:0] Input_bus_2,
  input  Reset,
  input  Clock,
  input  [3:0] HorizontalSpeed,
  input  ButtonLeft,
  input  ButtonRight,
  output [1:0] Output_bus_1,
  output ShowPlayer,
  output [7:0] Player,
  output [3:0] ReadAddr,
  output [3:0] PlayerLineNumber
);

  wire active, and_1_out, ButtonLeft_t, ButtonRight_t, Comp4_1_output_1, FallDownState, InitState,
       IsZero8_1_output_1, IsZero8_2_output_1, NextLine, not_1_out, not_2_out, not_3_out, not_4_out,
       not_5_out, or_1_out, or_2_out, or_3_out, or_5_out, PlayerBlockedBelow, PlayerIsBlocked_1_output_1,
       PlayerIsBlocked_2_output_1, PlayerIsBlocked_3_output_1, PlayerMoveState;
  wire [1:0] LocalState, MUX2x2_1_output_bus_1, MUX2x2_2_output_bus_1, MUX4x2_1_output_bus_1, NextLocalState;
  wire [2:0] random_1_out;
  wire [3:0] Inc4bit_2_output_bus_1, MUX2x4_2_output_bus_1, NextLineNumber, register_1_q;
  wire [7:0] MUX2x8_1_output_bus_1, MUX2x8_2_output_bus_1, MUX2x8_3_output_bus_1, PlayerLeft, PlayerRight,
       RandomPlayer;

  Comp2 Comp2_1 (.Input_bus_1(Input_bus_1), .Input_bus_2(2'b00), .Output_1(active));
  MUX2x2 MUX2x2_1 (
    .Input_bus_2(LocalState), .Input_bus_1(NextLocalState), .Input_1(NextLine),
    .Output_bus_1(MUX2x2_1_output_bus_1));
  MUX2x4 MUX2x4_1 (
    .Input_bus_2(PlayerLineNumber), .Input_bus_1(NextLineNumber), .Input_1(FallDownState),
    .Output_bus_1(ReadAddr));
  D_Flip_Flop d_ff_1 (.D(1'b0), .clk(Clock), .Q(ButtonLeft_t), .preset(ButtonLeft));  // open: Qn, reset
  D_Flip_Flop d_ff_2 (.D(1'b0), .clk(Clock), .Q(ButtonRight_t), .preset(ButtonRight));  // open: Qn, reset
  MUX4x2 MUX4x2_1 (
    .Input_bus_4(NextLocalState), .Input_bus_2(MUX2x2_1_output_bus_1), .Input_bus_5(2'b01),
    .Input_bus_3(LocalState), .Output_bus_1(MUX4x2_1_output_bus_1));  // open: Input_bus_1
  Register #(.width(2)) LocalStateVariable (
    .D(MUX4x2_1_output_bus_1), .en(1'b1), .clk(Clock), .Q(LocalState), .clr(not_1_out));
  not not_1 (not_1_out, active);
  DMX4x1 DMX4x1_1 (
    .Input_bus_1(LocalState), .Output_1(InitState), .Output_2(PlayerMoveState), .Output_3(FallDownState),
    .Input_1(active));  // open: Output_4
  Inc2bit Inc2bit_1 (.Input_bus_1(LocalState), .Output_bus_1(NextLocalState));
  IsZero8 IsZero8_1 (.Input_bus_1(PlayerRight), .Output_1(IsZero8_1_output_1));
  PlayerIsBlocked PlayerIsBlocked_1 (
    .Input_bus_1(PlayerRight), .Input_bus_2(Input_bus_2), .Output_1(PlayerIsBlocked_1_output_1));
  not not_2 (not_2_out, ButtonRight_t);
  MUX2x8 MUX2x8_1 (
    .Input_bus_2(PlayerRight), .Input_bus_1(Player), .Input_1(or_1_out), .Output_bus_1(MUX2x8_1_output_bus_1));
  or or_1 (or_1_out, IsZero8_1_output_1, PlayerIsBlocked_1_output_1, not_2_out);
  Register #(.width(4)) register_1 (
    .D(Inc4bit_2_output_bus_1), .en(1'b1), .clk(Clock), .Q(register_1_q), .clr(not_3_out));
  Inc4bit Inc4bit_2 (.Input_bus_1(register_1_q), .Output_bus_1(Inc4bit_2_output_bus_1));
  not not_3 (not_3_out, PlayerMoveState);
  Comp4 Comp4_2 (.Input_bus_2(register_1_q), .Input_bus_1(HorizontalSpeed), .Output_1(NextLine));
  IsZero8 IsZero8_2 (.Input_bus_1(PlayerLeft), .Output_1(IsZero8_2_output_1));
  not not_4 (not_4_out, ButtonLeft_t);
  MUX2x2 MUX2x2_2 (
    .Input_bus_2(2'b00), .Input_bus_1(2'b01), .Input_1(PlayerBlockedBelow),
    .Output_bus_1(MUX2x2_2_output_bus_1));
  or or_2 (or_2_out, IsZero8_2_output_1, PlayerIsBlocked_2_output_1, not_4_out);
  PlayerIsBlocked PlayerIsBlocked_2 (
    .Input_bus_1(PlayerLeft), .Input_bus_2(Input_bus_2), .Output_1(PlayerIsBlocked_2_output_1));
  MUX2x4 MUX2x4_2 (
    .Input_bus_2(PlayerLineNumber), .Input_bus_1(NextLineNumber), .Input_1(not_5_out),
    .Output_bus_1(MUX2x4_2_output_bus_1));
  not not_5 (not_5_out, PlayerBlockedBelow);
  MUX2x8 MUX2x8_3 (
    .Input_bus_2(PlayerLeft), .Input_bus_1(MUX2x8_1_output_bus_1), .Input_1(or_2_out),
    .Output_bus_1(MUX2x8_3_output_bus_1));
  and and_1 (and_1_out, not_5_out, FallDownState);
  MUX4x2 MUX4x2_2 (
    .Input_bus_4(2'b00), .Input_bus_2(2'b00), .Input_bus_5(MUX2x2_2_output_bus_1), .Input_bus_3(LocalState),
    .Output_bus_1(Output_bus_1));  // open: Input_bus_1
  Random #(.width(3)) random_1 (.clr(1'b0), .next(InitState), .clk(Clock), .out(random_1_out));
  Register #(.width(4)) register_2 (
    .D(MUX2x4_2_output_bus_1), .en(and_1_out), .clk(Clock), .Q(PlayerLineNumber), .clr(or_5_out));
  MUX2x8 MUX2x8_2 (
    .Input_bus_2(MUX2x8_3_output_bus_1), .Input_bus_1(RandomPlayer), .Input_1(InitState),
    .Output_bus_1(MUX2x8_2_output_bus_1));
  or or_3 (or_3_out, InitState, PlayerMoveState);
  PlayerIsBlocked PlayerIsBlocked_3 (
    .Input_bus_1(Input_bus_2), .Input_bus_2(Player), .Output_1(PlayerIsBlocked_3_output_1));
  or or_4 (PlayerBlockedBelow, PlayerIsBlocked_3_output_1, Comp4_1_output_1);
  Comp4 Comp4_1 (.Input_bus_2(PlayerLineNumber), .Input_bus_1(4'b1011), .Output_1(Comp4_1_output_1));
  or or_5 (or_5_out, InitState, Reset);
  DMX8x1 DMX8x1_1 (
    .Input_1(1'b1), .Input_bus_1(random_1_out), .Output_4(RandomPlayer[0]), .Output_8(RandomPlayer[1]),
    .Output_7(RandomPlayer[2]), .Output_1(RandomPlayer[3]), .Output_6(RandomPlayer[4]),
    .Output_3(RandomPlayer[5]), .Output_5(RandomPlayer[6]), .Output_2(RandomPlayer[7]));
  Register register_3 (.D(MUX2x8_2_output_bus_1), .en(or_3_out), .clk(Clock), .Q(Player), .clr(Reset));
  Inc4bit Inc4bit_1 (.Input_bus_1(PlayerLineNumber), .Output_bus_1(NextLineNumber));
  nand nand_1 (ShowPlayer, InitState, active);
  LeftShift8 LeftShift8_1 (.Input_bus_1(Player), .Output_bus_1(PlayerLeft));
  RightShift8 RightShift8_1 (.Input_bus_1(Player), .Output_bus_1(PlayerRight));

  // Other names for the same wires on the sheet: CurrentLineNumber[3:0] = PlayerLineNumber; PlayerReset = Reset;
  //   ReadLine[7:0] = Input_bus_2

  // Notes on the sheet:
  //   current state
  //   allow several horizontal steps before falling down
  //   Increase line number when in NOT blocket AND in FalldownState
  //   PlayerState
  //   BlockWriteState
  //   PlayerMoveCircuit
  //   next state
  //   LineHandlingCircuit
  //   At state 0 reset the line
endmodule

module player_fsm (
  input  right_button,
  input  left_button,
  input  [3:0] nb_side,
  input  [7:0] data_line,
  input  [1:0] current_state2,
  input  reset,
  input  clock,
  output [7:0] player2,
  output [3:0] read_line,
  output [3:0] player_line,
  output [1:0] next_state2
);

  wire or_1_out, set_next_state_1_active, set_next_state_1_reset_state;
  wire [2:0] blocked_1_next_state, line_nbr_plus_1_next_state, MUX6x3_1_output_bus_1, player_1_next_state,
       read_current_line_1_next_state, read_next_line_1_next_state, register_1_q,
       set_next_state_1_next_state3;
  wire [3:0] read_current_line_1_line_out, read_next_line_1_line_out;
  wire [7:0] read_current_line_1_data_out, read_next_line_1_data_out;

  // Probe on player_line
  read_current_line read_current_line_1 (
    .current_state(register_1_q), .clock(clock), .data_in(data_line), .reset(reset), .line_in(player_line),
    .next_state(read_current_line_1_next_state), .data_out(read_current_line_1_data_out),
    .line_out(read_current_line_1_line_out));
  read_next_line read_next_line_1 (
    .current_state(register_1_q), .clock(clock), .data_in(data_line), .reset(reset), .line_in(player_line),
    .next_state(read_next_line_1_next_state), .data_out(read_next_line_1_data_out),
    .line_out(read_next_line_1_line_out));
  line_nbr_plus line_nbr_plus_1 (
    .reset(reset), .current_state(register_1_q), .next_state(line_nbr_plus_1_next_state),
    .line_nbr(player_line));
  // Probe on player2
  player player_1 (
    .data_line(read_current_line_1_data_out), .right_button(right_button), .left_button(left_button),
    .clock(clock), .reset(reset), .nb_side(nb_side), .current_state(register_1_q), .player_out(player2),
    .next_state(player_1_next_state));
  blocked blocked_1 (
    .player(player2), .next_line(read_next_line_1_data_out), .current_state(register_1_q),
    .next_state(blocked_1_next_state), .line_nbr(player_line));
  set_next_state set_next_state_1 (
    .current_state3(register_1_q), .reset(reset), .clock(clock), .current_state2(current_state2),
    .next_state3(set_next_state_1_next_state3), .duplicate_state2(next_state2),
    .active(set_next_state_1_active), .reset_state(set_next_state_1_reset_state));
  // Probe on player_1_next_state
  // Probe on read_next_line_1_next_state
  // Probe on blocked_1_next_state
  // Probe on line_nbr_plus_1_next_state
  // Probe on set_next_state_1_next_state3
  // Probe on read_current_line_1_next_state
  // Probe on register_1_q
  // Probe on MUX6x3_1_output_bus_1
  MUX6x3 MUX6x3_1 (
    .Input_bus_1(read_current_line_1_next_state), .Input_bus_4(player_1_next_state),
    .Input_bus_3(read_next_line_1_next_state), .Input_bus_5(blocked_1_next_state),
    .Input_bus_2(line_nbr_plus_1_next_state), .Input_bus_6(set_next_state_1_next_state3),
    .current_state(register_1_q), .Output_bus_1(MUX6x3_1_output_bus_1));
  Register #(.width(3)) register_1 (
    .D(MUX6x3_1_output_bus_1), .en(set_next_state_1_active), .clk(clock), .Q(register_1_q), .clr(or_1_out));
  or or_1 (or_1_out, set_next_state_1_reset_state, reset);
  assign read_line = read_current_line_1_line_out | read_next_line_1_line_out;  // OR_Gate or_2, 4 bits wide
endmodule

module BlockWriteState (
  input  [1:0] Input_bus_2,
  input  Input_1,
  input  [7:0] ReadLine,
  input  [7:0] Player,
  input  [3:0] Input_bus_1,
  output [1:0] Output_bus_1,
  output Output_1,
  output [7:0] WriteData,
  output [3:0] Output_bus_2,
  output [3:0] Output_bus_3
);

  wire active, Comp2_1_output_1, GameOver, IsZero8_1_output_1, LineFull, not_1_out;
  wire [1:0] Inc2bit_1_output_bus_1, LocalState, MUX2x2_1_output_bus_1, MUX2x2_2_output_bus_1;
  wire [7:0] or_1_out, xor_1_out;

  Comp2 Comp2_2 (.Input_bus_1(Input_bus_2), .Input_bus_2(2'b01), .Output_1(active));
  Register #(.width(2)) register_1 (
    .D(Inc2bit_1_output_bus_1), .en(1'b1), .clk(Input_1), .Q(LocalState), .clr(not_1_out));
  Inc2bit Inc2bit_1 (.Input_bus_1(LocalState), .Output_bus_1(Inc2bit_1_output_bus_1));
  assign or_1_out = ReadLine | Player;  // OR_Gate or_1, 8 bits wide
  not not_1 (not_1_out, active);
  Comp4 Comp4_1 (.Input_bus_2(4'b0000), .Input_bus_1(Input_bus_1), .Output_1(GameOver));
  D_Flip_Flop d_ff_1 (.D(IsZero8_1_output_1), .clk(Input_1), .Q(LineFull));  // open: Qn, preset, reset
  IsZero8 IsZero8_1 (.Input_bus_1(xor_1_out), .Output_1(IsZero8_1_output_1));
  assign xor_1_out = {8{1'b1}} ^ or_1_out;  // XOR_Gate xor_1, 8 bits wide
  MUX2x2 MUX2x2_2 (.Input_bus_2(2'b01), .Input_bus_1(2'b11), .Input_1(GameOver), .Output_bus_1(MUX2x2_2_output_bus_1));
  MUX2x2 MUX2x2_1 (.Input_bus_2(2'b00), .Input_bus_1(2'b10), .Input_1(LineFull), .Output_bus_1(MUX2x2_1_output_bus_1));
  Comp2 Comp2_1 (.Input_bus_1(LocalState), .Input_bus_2(2'b00), .Output_1(Comp2_1_output_1));
  and and_1 (Output_1, Comp2_1_output_1, active);
  MUX4x2 MUX4x2_1 (
    .Input_bus_4(MUX2x2_2_output_bus_1), .Input_bus_2(MUX2x2_1_output_bus_1), .Input_bus_5(2'b00),
    .Input_bus_1(2'b00), .Input_bus_3(LocalState), .Output_bus_1(Output_bus_1));

  assign Output_bus_2 = Input_bus_1;
  assign Output_bus_3 = Input_bus_1;
  assign WriteData = Player;

  // Other names for the same wires on the sheet: clock = Input_1

  // Notes on the sheet:
  //   clock
  //   current state
  //   line number
  //   second phase: read line from memory
  //   local state variable
  //   If first line, then game over
  //   write addr
  //   read addr
  //   PlayerState
  //   LineDeleteState
  //   third phase: choose next state
  //   first phase: write block to memory
  //   WriteEnable
  //   next state
endmodule

module ScorePointState (
  input  [1:0] Input_bus_1,
  input  [1:0] clock_div,
  input  Input_1,
  input  ScoreReset,
  output [1:0] Output_bus_1,
  output Output_1,
  output Output_2,
  output [7:0] Score
);

  wire active, and_1_out, ClockDiv_1_output_1, Comp2_1_output_1, Comp3_1_output_1, d_ff_1_q, IncState,
       not_1_out, not_2_out;
  wire [1:0] Inc2bit_1_output_bus_1, LocalState, MUX2x2_1_output_bus_1;
  wire [2:0] Inc3bit_1_output_bus_1, register_2_q;

  Inc2bit Inc2bit_1 (.Input_bus_1(LocalState), .Output_bus_1(Inc2bit_1_output_bus_1));
  Comp2 Comp2_2 (.Input_bus_1(Input_bus_1), .Input_bus_2(2'b10), .Output_1(active));
  Register #(.width(2)) register_1 (
    .D(MUX2x2_1_output_bus_1), .en(1'b1), .clk(Input_1), .Q(LocalState), .clr(not_1_out));
  // Probe on MUX2x2_1_output_bus_1
  MUX2x2 MUX2x2_1 (
    .Input_bus_2(LocalState), .Input_bus_1(Inc2bit_1_output_bus_1), .Input_1(IncState),
    .Output_bus_1(MUX2x2_1_output_bus_1));
  not not_1 (not_1_out, active);
  Comp2 Comp2_1 (.Input_bus_1(LocalState), .Input_bus_2(2'b00), .Output_1(Comp2_1_output_1));
  ClockDiv ClockDiv_1 (.Input_1(Input_1), .Input_bus_1(clock_div), .Output_1(ClockDiv_1_output_1));
  and and_1 (and_1_out, Comp2_1_output_1, active);
  Register #(.width(3)) register_2 (
    .D(Inc3bit_1_output_bus_1), .en(and_1_out), .clk(ClockDiv_1_output_1), .Q(register_2_q), .clr(not_2_out));
  Inc3bit Inc3bit_1 (.Input_bus_1(register_2_q), .Output_bus_1(Inc3bit_1_output_bus_1));
  not not_2 (not_2_out, and_1_out);
  Comp2 Comp2_3 (.Input_bus_1(LocalState), .Input_bus_2(2'b01), .Output_1(Output_2));
  MUX4x2 MUX4x2_1 (
    .Input_bus_4(2'b10), .Input_bus_2(2'b10), .Input_bus_5(2'b00), .Input_bus_3(LocalState),
    .Output_bus_1(Output_bus_1));  // open: Input_bus_1
  Comp3 Comp3_1 (.Input_bus_2(register_2_q), .Input_bus_1(3'b101), .Output_1(Comp3_1_output_1));
  ScoreCounter ScoreCounter_1 (.Input_1(Output_2), .Input_2(ScoreReset), .Output_bus_1(Score));
  D_Flip_Flop d_ff_1 (
    .D(Comp3_1_output_1), .clk(ClockDiv_1_output_1), .Q(d_ff_1_q), .reset(not_2_out));  // open: Qn, preset
  and and_2 (Output_1, and_1_out, register_2_q[0]);
  or or_1 (IncState, d_ff_1_q, Output_2);

  // Other names for the same wires on the sheet: Clock = Input_1

  // Notes on the sheet:
  //   current state
  //   clock
  //   local state variable
  //   line shift
  //   blink
  //   next state
  //   line blink
endmodule

module ScoreCounter (
  input  Input_1,
  input  Input_2,
  output [7:0] Output_bus_1
);

  wire Comp4_1_output_1;
  wire [3:0] Inc4bit_1_output_bus_1, Inc4bit_2_output_bus_1, MUX2x4_1_output_bus_1;

  Inc4bit Inc4bit_2 (.Input_bus_1(Output_bus_1[3:0]), .Output_bus_1(Inc4bit_2_output_bus_1));
  Comp4 Comp4_1 (.Input_bus_2(Inc4bit_2_output_bus_1), .Input_bus_1(4'b1010), .Output_1(Comp4_1_output_1));
  MUX2x4 MUX2x4_1 (
    .Input_bus_2(Inc4bit_2_output_bus_1), .Input_bus_1(4'b0000), .Input_1(Comp4_1_output_1),
    .Output_bus_1(MUX2x4_1_output_bus_1));
  Register #(.width(4)) register_1 (
    .D(MUX2x4_1_output_bus_1), .en(1'b1), .clk(Input_1), .Q(Output_bus_1[3:0]), .clr(Input_2));
  Inc4bit Inc4bit_1 (.Input_bus_1(Output_bus_1[7:4]), .Output_bus_1(Inc4bit_1_output_bus_1));
  Register #(.width(4)) register_2 (
    .D(Inc4bit_1_output_bus_1), .en(Comp4_1_output_1), .clk(Input_1), .Q(Output_bus_1[7:4]), .clr(Input_2));

  // Notes on the sheet:
  //   clock
  //   score reset
  //   score low
  //   score high
endmodule

module GameOverState (
  input  [1:0] Input_bus_14,
  input  Input_1,
  input  Input_2,
  input  Clock,
  input  [7:0] Input_bus_1,
  input  [7:0] Input_bus_9,
  input  [7:0] Input_bus_5,
  input  [7:0] Input_bus_2,
  input  [7:0] Input_bus_10,
  input  [7:0] Input_bus_12,
  input  [7:0] Input_bus_11,
  input  [7:0] Input_bus_3,
  input  [7:0] Input_bus_4,
  input  [7:0] Input_bus_6,
  input  [7:0] Input_bus_8,
  input  [7:0] Input_bus_13,
  input  [7:0] Input_bus_7,
  output [1:0] Output_bus_4,
  output Output_1,
  output [7:0] Output_bus_3,
  output [7:0] Output_bus_9,
  output [7:0] Output_bus_11,
  output [7:0] Output_bus_5,
  output [7:0] Output_bus_8,
  output [7:0] Output_bus_13,
  output [7:0] Output_bus_6,
  output [7:0] Output_bus_10,
  output [7:0] Output_bus_12,
  output [7:0] Output_bus_1,
  output [7:0] Output_bus_2,
  output [7:0] Output_bus_7
);

  wire active, and_1_out, d_ff_1_q, not_2_out, or_1_out;
  wire [7:0] display_number_1_four, display_number_1_one, display_number_1_three, display_number_1_two,
       display_number_1_zero, Mask12x8_1_output_bus_1, Mask12x8_1_output_bus_2, Mask12x8_1_output_bus_3,
       Mask12x8_1_output_bus_4, Mask12x8_1_output_bus_5, Mask12x8_1_output_bus_6, Mask12x8_1_output_bus_7,
       Mask12x8_1_output_bus_8, Mask12x8_1_output_bus_9, Mask12x8_1_output_bus_10, Mask12x8_1_output_bus_11,
       Mask12x8_1_output_bus_12, Mask12x8_2_output_bus_1, Mask12x8_2_output_bus_2, Mask12x8_2_output_bus_3,
       Mask12x8_2_output_bus_4, Mask12x8_2_output_bus_5, Mask12x8_2_output_bus_6, Mask12x8_2_output_bus_7,
       Mask12x8_2_output_bus_8, Mask12x8_2_output_bus_9, Mask12x8_2_output_bus_10, Mask12x8_2_output_bus_11,
       Mask12x8_2_output_bus_12;
  wire [11:11] not_1_out;

  Comp2 Comp2_1 (.Input_bus_1(Input_bus_14), .Input_bus_2(2'b11), .Output_1(active));
  not not_1 (not_1_out[11], active);
  or or_1 (or_1_out, Input_1, Input_2);
  display_number display_number_1 (
    .Zero(display_number_1_zero), .One(display_number_1_one), .Two(display_number_1_two),
    .Three(display_number_1_three), .Four(display_number_1_four), .High(Input_bus_1[7:4]),
    .Low(Input_bus_1[3:0]));
  Mask12x8 Mask12x8_2 (
    .Input_bus_10(Input_bus_9), .Input_bus_13(Input_bus_5), .Input_bus_5(Input_bus_2),
    .Input_bus_6(Input_bus_10), .Input_bus_4(Input_bus_12), .Input_bus_1(Input_bus_11),
    .Input_bus_2(Input_bus_3), .Input_bus_7(Input_bus_4), .Input_bus_9(Input_bus_6),
    .Input_bus_8(Input_bus_8), .Input_bus_3(Input_bus_13), .Input_bus_11(Input_bus_7),
    .Input_bus_12({12{not_1_out[11]}}), .Output_bus_10(Mask12x8_2_output_bus_10),
    .Output_bus_11(Mask12x8_2_output_bus_11), .Output_bus_4(Mask12x8_2_output_bus_4),
    .Output_bus_2(Mask12x8_2_output_bus_2), .Output_bus_12(Mask12x8_2_output_bus_12),
    .Output_bus_6(Mask12x8_2_output_bus_6), .Output_bus_8(Mask12x8_2_output_bus_8),
    .Output_bus_3(Mask12x8_2_output_bus_3), .Output_bus_5(Mask12x8_2_output_bus_5),
    .Output_bus_9(Mask12x8_2_output_bus_9), .Output_bus_1(Mask12x8_2_output_bus_1),
    .Output_bus_7(Mask12x8_2_output_bus_7));
  D_Flip_Flop d_ff_1 (.D(or_1_out), .clk(Clock), .Q(d_ff_1_q));  // open: Qn, preset, reset
  and and_1 (and_1_out, or_1_out, not_2_out);
  not not_2 (not_2_out, d_ff_1_q);
  Mask12x8 Mask12x8_1 (
    .Input_bus_10({8{1'b0}}), .Input_bus_13({8{1'b0}}), .Input_bus_5({8{1'b0}}),
    .Input_bus_6(display_number_1_zero), .Input_bus_4(display_number_1_one),
    .Input_bus_1(display_number_1_two), .Input_bus_2(display_number_1_three),
    .Input_bus_7(display_number_1_four), .Input_bus_9({8{1'b0}}), .Input_bus_8({8{1'b0}}),
    .Input_bus_3({8{1'b0}}), .Input_bus_11({8{1'b0}}), .Input_bus_12({12{active}}),
    .Output_bus_10(Mask12x8_1_output_bus_10), .Output_bus_11(Mask12x8_1_output_bus_11),
    .Output_bus_4(Mask12x8_1_output_bus_4), .Output_bus_2(Mask12x8_1_output_bus_2),
    .Output_bus_12(Mask12x8_1_output_bus_12), .Output_bus_6(Mask12x8_1_output_bus_6),
    .Output_bus_8(Mask12x8_1_output_bus_8), .Output_bus_3(Mask12x8_1_output_bus_3),
    .Output_bus_5(Mask12x8_1_output_bus_5), .Output_bus_9(Mask12x8_1_output_bus_9),
    .Output_bus_1(Mask12x8_1_output_bus_1), .Output_bus_7(Mask12x8_1_output_bus_7));
  OR12x8 OR12x8_1 (
    .Input_bus_22(Mask12x8_2_output_bus_10), .Input_bus_8(Mask12x8_2_output_bus_11),
    .Input_bus_6(Mask12x8_2_output_bus_4), .Input_bus_13(Mask12x8_2_output_bus_2),
    .Input_bus_4(Mask12x8_2_output_bus_12), .Input_bus_9(Mask12x8_2_output_bus_6),
    .Input_bus_19(Mask12x8_2_output_bus_8), .Input_bus_21(Mask12x8_2_output_bus_3),
    .Input_bus_5(Mask12x8_2_output_bus_5), .Input_bus_15(Mask12x8_2_output_bus_9),
    .Input_bus_3(Mask12x8_2_output_bus_1), .Input_bus_11(Mask12x8_2_output_bus_7),
    .Input_bus_24(Mask12x8_1_output_bus_10), .Input_bus_2(Mask12x8_1_output_bus_11),
    .Input_bus_1(Mask12x8_1_output_bus_4), .Input_bus_7(Mask12x8_1_output_bus_2),
    .Input_bus_17(Mask12x8_1_output_bus_12), .Input_bus_14(Mask12x8_1_output_bus_6),
    .Input_bus_20(Mask12x8_1_output_bus_8), .Input_bus_16(Mask12x8_1_output_bus_3),
    .Input_bus_10(Mask12x8_1_output_bus_5), .Input_bus_23(Mask12x8_1_output_bus_9),
    .Input_bus_12(Mask12x8_1_output_bus_1), .Input_bus_18(Mask12x8_1_output_bus_7),
    .Output_bus_5(Output_bus_3), .Output_bus_1(Output_bus_9), .Output_bus_8(Output_bus_11),
    .Output_bus_12(Output_bus_5), .Output_bus_3(Output_bus_8), .Output_bus_4(Output_bus_13),
    .Output_bus_9(Output_bus_6), .Output_bus_6(Output_bus_10), .Output_bus_7(Output_bus_12),
    .Output_bus_11(Output_bus_1), .Output_bus_10(Output_bus_2), .Output_bus_2(Output_bus_7));
  MUX2x2 MUX2x2_1 (.Input_bus_2(2'b11), .Input_bus_1(2'b00), .Input_1(and_1_out), .Output_bus_1(Output_bus_4));
  and and_2 (Output_1, and_1_out, active);

  // Notes on the sheet:
  //   current state
  //   score
  //   Button1
  //   Button2
  //   rising edge detector
  //   next state
  //   GameReset
endmodule

module DisplayDriver (
  input  [7:0] Input_bus_3,
  input  [3:0] Input_bus_2,
  input  [3:0] Input_bus_1,
  input  Input_4,
  input  Input_2,
  input  Input_3,
  input  Input_1,
  output [7:0] Output_bus_3,
  output [7:0] Output_bus_4,
  output [7:0] Output_bus_11,
  output [7:0] Output_bus_13,
  output [7:0] Output_bus_12,
  output [7:0] Output_bus_2,
  output [7:0] Output_bus_6,
  output [7:0] Output_bus_9,
  output [7:0] Output_bus_1,
  output [7:0] Output_bus_7,
  output [7:0] Output_bus_8,
  output [7:0] Output_bus_10,
  output [7:0] Output_bus_5
);

  wire [7:0] DMX12x8_1_output_bus_1, DMX12x8_1_output_bus_2, DMX12x8_1_output_bus_3, DMX12x8_1_output_bus_4,
       DMX12x8_1_output_bus_5, DMX12x8_1_output_bus_6, DMX12x8_1_output_bus_7, DMX12x8_1_output_bus_8,
       DMX12x8_1_output_bus_9, DMX12x8_1_output_bus_10, DMX12x8_1_output_bus_11, DMX12x8_1_output_bus_12;

  DMX12x8 DMX12x8_1 (
    .Input_bus_1(Input_bus_3), .Input_bus_2(Input_bus_2), .Output_bus_6(DMX12x8_1_output_bus_6),
    .Output_bus_9(DMX12x8_1_output_bus_9), .Output_bus_5(DMX12x8_1_output_bus_5),
    .Output_bus_8(DMX12x8_1_output_bus_8), .Output_bus_12(DMX12x8_1_output_bus_12),
    .Output_bus_1(DMX12x8_1_output_bus_1), .Output_bus_11(DMX12x8_1_output_bus_11),
    .Output_bus_7(DMX12x8_1_output_bus_7), .Output_bus_10(DMX12x8_1_output_bus_10),
    .Output_bus_2(DMX12x8_1_output_bus_2), .Output_bus_3(DMX12x8_1_output_bus_3),
    .Output_bus_4(DMX12x8_1_output_bus_4));
  BlockMemoryDriver BlockMemoryDriver_1 (
    .Input_3(Input_4), .Input_2(Input_3), .Input_4(Input_1), .Input_bus_7(DMX12x8_1_output_bus_6),
    .Input_bus_8(DMX12x8_1_output_bus_9), .Input_bus_3(DMX12x8_1_output_bus_5),
    .Input_bus_11(DMX12x8_1_output_bus_8), .Input_bus_6(DMX12x8_1_output_bus_12),
    .Input_bus_4(DMX12x8_1_output_bus_1), .Input_bus_9(DMX12x8_1_output_bus_11),
    .Input_bus_5(DMX12x8_1_output_bus_7), .Input_bus_12(DMX12x8_1_output_bus_10),
    .Input_bus_1(DMX12x8_1_output_bus_2), .Input_bus_2(DMX12x8_1_output_bus_3),
    .Input_bus_10(DMX12x8_1_output_bus_4), .Output_bus_6(Output_bus_3), .Output_bus_12(Output_bus_4),
    .Output_bus_10(Output_bus_11), .Output_bus_1(Output_bus_13), .Output_bus_7(Output_bus_12),
    .Output_bus_9(Output_bus_2), .Output_bus_4(Output_bus_6), .Output_bus_11(Output_bus_9),
    .Output_bus_8(Output_bus_1), .Output_bus_2(Output_bus_7), .Output_bus_3(Output_bus_8),
    .Output_bus_5(Output_bus_10), .Input_1(Input_2));
  MUX12x8 MUX12x8_1 (
    .Input_bus_3(Output_bus_3), .Input_bus_10(Output_bus_4), .Input_bus_8(Output_bus_11),
    .Input_bus_11(Output_bus_13), .Input_bus_2(Output_bus_12), .Input_bus_12(Output_bus_2),
    .Input_bus_4(Output_bus_6), .Input_bus_7(Output_bus_9), .Input_bus_5(Output_bus_1),
    .Input_bus_6(Output_bus_7), .Input_bus_9(Output_bus_8), .Input_bus_13(Output_bus_10),
    .Input_bus_1(Input_bus_1), .Output_bus_1(Output_bus_5));

  // Notes on the sheet:
  //   write line data
  //   write line number
  //   read line number
  //   line shift
  //   Clock
  //   write enable
  //   Reset
  //   Display output
  //   read line data
endmodule

module BlockMemory (
  input  Input_1,
  input  Input_3,
  input  Input_2,
  input  [7:0] Input_bus_3,
  input  [7:0] Input_bus_9,
  input  [7:0] Input_bus_12,
  input  [7:0] Input_bus_1,
  input  [7:0] Input_bus_4,
  input  [7:0] Input_bus_11,
  input  [7:0] Input_bus_8,
  input  [7:0] Input_bus_6,
  input  [7:0] Input_bus_2,
  input  [7:0] Input_bus_10,
  input  [7:0] Input_bus_7,
  input  [7:0] Input_bus_5,
  output [7:0] Output_bus_8,
  output [7:0] Output_bus_7,
  output [7:0] Output_bus_11,
  output [7:0] Output_bus_5,
  output [7:0] Output_bus_3,
  output [7:0] Output_bus_4,
  output [7:0] Output_bus_12,
  output [7:0] Output_bus_2,
  output [7:0] Output_bus_9,
  output [7:0] Output_bus_10,
  output [7:0] Output_bus_6,
  output [7:0] Output_bus_1
);

  Register register_1 (.D(Input_bus_3), .en(Input_1), .clk(Input_3), .Q(Output_bus_8), .clr(Input_2));
  Register register_2 (.D(Input_bus_9), .en(Input_1), .clk(Input_3), .Q(Output_bus_7), .clr(Input_2));
  Register register_3 (.D(Input_bus_12), .en(Input_1), .clk(Input_3), .Q(Output_bus_11), .clr(Input_2));
  Register register_4 (.D(Input_bus_1), .en(Input_1), .clk(Input_3), .Q(Output_bus_5), .clr(Input_2));
  Register register_5 (.D(Input_bus_4), .en(Input_1), .clk(Input_3), .Q(Output_bus_3), .clr(Input_2));
  Register register_6 (.D(Input_bus_11), .en(Input_1), .clk(Input_3), .Q(Output_bus_4), .clr(Input_2));
  Register register_7 (.D(Input_bus_8), .en(Input_1), .clk(Input_3), .Q(Output_bus_12), .clr(Input_2));
  Register register_8 (.D(Input_bus_6), .en(Input_1), .clk(Input_3), .Q(Output_bus_2), .clr(Input_2));
  Register register_9 (.D(Input_bus_2), .en(Input_1), .clk(Input_3), .Q(Output_bus_9), .clr(Input_2));
  Register register_10 (.D(Input_bus_10), .en(Input_1), .clk(Input_3), .Q(Output_bus_10), .clr(Input_2));
  Register register_11 (.D(Input_bus_7), .en(Input_1), .clk(Input_3), .Q(Output_bus_6), .clr(Input_2));
  Register register_12 (.D(Input_bus_5), .en(Input_1), .clk(Input_3), .Q(Output_bus_1), .clr(Input_2));

  // Notes on the sheet:
  //   WE
  //   CLK
  //   Reset
endmodule

module BlockMemoryDriver (
  input  [7:0] Input_bus_7,
  input  [7:0] Input_bus_8,
  input  [7:0] Input_bus_3,
  input  [7:0] Input_bus_11,
  input  [7:0] Input_bus_6,
  input  [7:0] Input_bus_4,
  input  [7:0] Input_bus_9,
  input  [7:0] Input_bus_5,
  input  [7:0] Input_bus_12,
  input  [7:0] Input_bus_1,
  input  [7:0] Input_bus_2,
  input  [7:0] Input_bus_10,
  input  Input_3,
  input  Input_2,
  input  Input_4,
  input  Input_1,
  output [7:0] Output_bus_6,
  output [7:0] Output_bus_12,
  output [7:0] Output_bus_10,
  output [7:0] Output_bus_1,
  output [7:0] Output_bus_7,
  output [7:0] Output_bus_9,
  output [7:0] Output_bus_4,
  output [7:0] Output_bus_11,
  output [7:0] Output_bus_8,
  output [7:0] Output_bus_2,
  output [7:0] Output_bus_3,
  output [7:0] Output_bus_5
);

  wire or_1_out;
  wire [7:0] Mask12x8_1_output_bus_1, Mask12x8_1_output_bus_2, Mask12x8_1_output_bus_3,
       Mask12x8_1_output_bus_4, Mask12x8_1_output_bus_5, Mask12x8_1_output_bus_6, Mask12x8_1_output_bus_7,
       Mask12x8_1_output_bus_8, Mask12x8_1_output_bus_9, Mask12x8_1_output_bus_10, Mask12x8_1_output_bus_11,
       Mask12x8_1_output_bus_12, Mask12x8_2_output_bus_1, Mask12x8_2_output_bus_2, Mask12x8_2_output_bus_3,
       Mask12x8_2_output_bus_4, Mask12x8_2_output_bus_5, Mask12x8_2_output_bus_6, Mask12x8_2_output_bus_8,
       Mask12x8_2_output_bus_9, Mask12x8_2_output_bus_10, Mask12x8_2_output_bus_11, Mask12x8_2_output_bus_12,
       OR12x8_1_output_bus_1, OR12x8_1_output_bus_2, OR12x8_1_output_bus_3, OR12x8_1_output_bus_4,
       OR12x8_1_output_bus_5, OR12x8_1_output_bus_6, OR12x8_1_output_bus_7, OR12x8_1_output_bus_8,
       OR12x8_1_output_bus_9, OR12x8_1_output_bus_10, OR12x8_1_output_bus_11, OR12x8_1_output_bus_12,
       OR12x8_2_output_bus_1, OR12x8_2_output_bus_2, OR12x8_2_output_bus_3, OR12x8_2_output_bus_4,
       OR12x8_2_output_bus_5, OR12x8_2_output_bus_6, OR12x8_2_output_bus_7, OR12x8_2_output_bus_8,
       OR12x8_2_output_bus_9, OR12x8_2_output_bus_10, OR12x8_2_output_bus_11, OR12x8_2_output_bus_12;
  wire [11:0] not_1_out;

  OR12x8 OR12x8_2 (
    .Input_bus_22(Input_bus_7), .Input_bus_8(Input_bus_8), .Input_bus_6(Input_bus_3),
    .Input_bus_13(Input_bus_11), .Input_bus_4(Input_bus_6), .Input_bus_9(Input_bus_4),
    .Input_bus_19(Input_bus_9), .Input_bus_21(Input_bus_5), .Input_bus_5(Input_bus_12),
    .Input_bus_15(Input_bus_1), .Input_bus_3(Input_bus_2), .Input_bus_11(Input_bus_10),
    .Input_bus_24(Output_bus_6), .Input_bus_2(Output_bus_12), .Input_bus_1(Output_bus_10),
    .Input_bus_7(Output_bus_1), .Input_bus_17(Output_bus_7), .Input_bus_14(Output_bus_9),
    .Input_bus_20(Output_bus_4), .Input_bus_16(Output_bus_11), .Input_bus_10(Output_bus_8),
    .Input_bus_23(Output_bus_2), .Input_bus_12(Output_bus_3), .Input_bus_18(Output_bus_5),
    .Output_bus_5(OR12x8_2_output_bus_5), .Output_bus_1(OR12x8_2_output_bus_1),
    .Output_bus_8(OR12x8_2_output_bus_8), .Output_bus_12(OR12x8_2_output_bus_12),
    .Output_bus_3(OR12x8_2_output_bus_3), .Output_bus_4(OR12x8_2_output_bus_4),
    .Output_bus_9(OR12x8_2_output_bus_9), .Output_bus_6(OR12x8_2_output_bus_6),
    .Output_bus_7(OR12x8_2_output_bus_7), .Output_bus_11(OR12x8_2_output_bus_11),
    .Output_bus_10(OR12x8_2_output_bus_10), .Output_bus_2(OR12x8_2_output_bus_2));
  or or_1 (or_1_out, Input_3, Input_2);
  Mask12x8 Mask12x8_1 (
    .Input_bus_10(OR12x8_2_output_bus_5), .Input_bus_13(OR12x8_2_output_bus_1),
    .Input_bus_5(OR12x8_2_output_bus_8), .Input_bus_6(OR12x8_2_output_bus_12),
    .Input_bus_4(OR12x8_2_output_bus_3), .Input_bus_1(OR12x8_2_output_bus_4),
    .Input_bus_2(OR12x8_2_output_bus_9), .Input_bus_7(OR12x8_2_output_bus_6),
    .Input_bus_9(OR12x8_2_output_bus_7), .Input_bus_8(OR12x8_2_output_bus_11),
    .Input_bus_3(OR12x8_2_output_bus_10), .Input_bus_11(OR12x8_2_output_bus_2), .Input_bus_12(not_1_out),
    .Output_bus_10(Mask12x8_1_output_bus_10), .Output_bus_11(Mask12x8_1_output_bus_11),
    .Output_bus_4(Mask12x8_1_output_bus_4), .Output_bus_2(Mask12x8_1_output_bus_2),
    .Output_bus_12(Mask12x8_1_output_bus_12), .Output_bus_6(Mask12x8_1_output_bus_6),
    .Output_bus_8(Mask12x8_1_output_bus_8), .Output_bus_3(Mask12x8_1_output_bus_3),
    .Output_bus_5(Mask12x8_1_output_bus_5), .Output_bus_9(Mask12x8_1_output_bus_9),
    .Output_bus_1(Mask12x8_1_output_bus_1), .Output_bus_7(Mask12x8_1_output_bus_7));
  assign not_1_out = ~{12{Input_3}};  // NOT_Gate not_1, 12 bits wide
  Mask12x8 Mask12x8_2 (
    .Input_bus_10(Output_bus_6), .Input_bus_13(Output_bus_12), .Input_bus_5(Output_bus_10),
    .Input_bus_6(Output_bus_1), .Input_bus_4(Output_bus_7), .Input_bus_1(Output_bus_9),
    .Input_bus_2(Output_bus_4), .Input_bus_7(Output_bus_11), .Input_bus_9(Output_bus_8),
    .Input_bus_8(Output_bus_2), .Input_bus_3(Output_bus_3), .Input_bus_11(Output_bus_5),
    .Input_bus_12({12{Input_3}}), .Output_bus_10(Mask12x8_2_output_bus_10),
    .Output_bus_11(Mask12x8_2_output_bus_11), .Output_bus_4(Mask12x8_2_output_bus_4),
    .Output_bus_2(Mask12x8_2_output_bus_2), .Output_bus_12(Mask12x8_2_output_bus_12),
    .Output_bus_6(Mask12x8_2_output_bus_6), .Output_bus_8(Mask12x8_2_output_bus_8),
    .Output_bus_3(Mask12x8_2_output_bus_3), .Output_bus_5(Mask12x8_2_output_bus_5),
    .Output_bus_9(Mask12x8_2_output_bus_9), .Output_bus_1(Mask12x8_2_output_bus_1));  // open: Output_bus_7
  OR12x8 OR12x8_1 (
    .Input_bus_22(Mask12x8_1_output_bus_10), .Input_bus_8(Mask12x8_1_output_bus_11),
    .Input_bus_6(Mask12x8_1_output_bus_4), .Input_bus_13(Mask12x8_1_output_bus_2),
    .Input_bus_4(Mask12x8_1_output_bus_12), .Input_bus_9(Mask12x8_1_output_bus_6),
    .Input_bus_19(Mask12x8_1_output_bus_8), .Input_bus_21(Mask12x8_1_output_bus_3),
    .Input_bus_5(Mask12x8_1_output_bus_5), .Input_bus_15(Mask12x8_1_output_bus_9),
    .Input_bus_3(Mask12x8_1_output_bus_1), .Input_bus_11(Mask12x8_1_output_bus_7), .Input_bus_24({8{1'b0}}),
    .Input_bus_2(Mask12x8_2_output_bus_10), .Input_bus_1(Mask12x8_2_output_bus_11),
    .Input_bus_7(Mask12x8_2_output_bus_4), .Input_bus_17(Mask12x8_2_output_bus_2),
    .Input_bus_14(Mask12x8_2_output_bus_12), .Input_bus_20(Mask12x8_2_output_bus_6),
    .Input_bus_16(Mask12x8_2_output_bus_8), .Input_bus_10(Mask12x8_2_output_bus_3),
    .Input_bus_23(Mask12x8_2_output_bus_5), .Input_bus_12(Mask12x8_2_output_bus_9),
    .Input_bus_18(Mask12x8_2_output_bus_1), .Output_bus_5(OR12x8_1_output_bus_5),
    .Output_bus_1(OR12x8_1_output_bus_1), .Output_bus_8(OR12x8_1_output_bus_8),
    .Output_bus_12(OR12x8_1_output_bus_12), .Output_bus_3(OR12x8_1_output_bus_3),
    .Output_bus_4(OR12x8_1_output_bus_4), .Output_bus_9(OR12x8_1_output_bus_9),
    .Output_bus_6(OR12x8_1_output_bus_6), .Output_bus_7(OR12x8_1_output_bus_7),
    .Output_bus_11(OR12x8_1_output_bus_11), .Output_bus_10(OR12x8_1_output_bus_10),
    .Output_bus_2(OR12x8_1_output_bus_2));
  BlockMemory BlockMemory_1 (
    .Input_1(or_1_out), .Input_3(Input_1), .Input_2(Input_4), .Input_bus_3(OR12x8_1_output_bus_5),
    .Input_bus_9(OR12x8_1_output_bus_1), .Input_bus_12(OR12x8_1_output_bus_8),
    .Input_bus_1(OR12x8_1_output_bus_12), .Input_bus_4(OR12x8_1_output_bus_3),
    .Input_bus_11(OR12x8_1_output_bus_4), .Input_bus_8(OR12x8_1_output_bus_9),
    .Input_bus_6(OR12x8_1_output_bus_6), .Input_bus_2(OR12x8_1_output_bus_7),
    .Input_bus_10(OR12x8_1_output_bus_11), .Input_bus_7(OR12x8_1_output_bus_10),
    .Input_bus_5(OR12x8_1_output_bus_2), .Output_bus_8(Output_bus_6), .Output_bus_7(Output_bus_12),
    .Output_bus_11(Output_bus_10), .Output_bus_5(Output_bus_1), .Output_bus_3(Output_bus_7),
    .Output_bus_4(Output_bus_9), .Output_bus_12(Output_bus_4), .Output_bus_2(Output_bus_11),
    .Output_bus_9(Output_bus_8), .Output_bus_10(Output_bus_2), .Output_bus_6(Output_bus_3),
    .Output_bus_1(Output_bus_5));

  // Notes on the sheet:
  //   line shift
  //   write enable
  //   Reset
  //   Clock
endmodule

module DrawPlayer (
  input  [7:0] Player,
  input  ShowPlayer,
  input  [3:0] PlayerLine,
  input  [7:0] Input_bus_11,
  input  [7:0] Input_bus_8,
  input  [7:0] Input_bus_9,
  input  [7:0] Input_bus_6,
  input  [7:0] Input_bus_1,
  input  [7:0] Input_bus_12,
  input  [7:0] Input_bus_2,
  input  [7:0] Input_bus_3,
  input  [7:0] Input_bus_4,
  input  [7:0] Input_bus_5,
  input  [7:0] Input_bus_7,
  input  [7:0] Input_bus_10,
  output [7:0] Output_bus_1,
  output [7:0] Output_bus_3,
  output [7:0] Output_bus_2,
  output [7:0] Output_bus_5,
  output [7:0] Output_bus_10,
  output [7:0] Output_bus_7,
  output [7:0] Output_bus_4,
  output [7:0] Output_bus_9,
  output [7:0] Output_bus_11,
  output [7:0] Output_bus_8,
  output [7:0] Output_bus_6,
  output [7:0] Output_bus_12
);

  wire [7:0] DMX12x8_1_output_bus_1, DMX12x8_1_output_bus_2, DMX12x8_1_output_bus_3, DMX12x8_1_output_bus_4,
       DMX12x8_1_output_bus_5, DMX12x8_1_output_bus_6, DMX12x8_1_output_bus_7, DMX12x8_1_output_bus_8,
       DMX12x8_1_output_bus_9, DMX12x8_1_output_bus_10, DMX12x8_1_output_bus_11, DMX12x8_1_output_bus_12,
       Mask8bit_1_output_bus_1;

  Mask8bit Mask8bit_1 (.Input_bus_1(Player), .Input_1(ShowPlayer), .Output_bus_1(Mask8bit_1_output_bus_1));
  DMX12x8 DMX12x8_1 (
    .Input_bus_1(Mask8bit_1_output_bus_1), .Input_bus_2(PlayerLine), .Output_bus_6(DMX12x8_1_output_bus_6),
    .Output_bus_9(DMX12x8_1_output_bus_9), .Output_bus_5(DMX12x8_1_output_bus_5),
    .Output_bus_8(DMX12x8_1_output_bus_8), .Output_bus_12(DMX12x8_1_output_bus_12),
    .Output_bus_1(DMX12x8_1_output_bus_1), .Output_bus_11(DMX12x8_1_output_bus_11),
    .Output_bus_7(DMX12x8_1_output_bus_7), .Output_bus_10(DMX12x8_1_output_bus_10),
    .Output_bus_2(DMX12x8_1_output_bus_2), .Output_bus_3(DMX12x8_1_output_bus_3),
    .Output_bus_4(DMX12x8_1_output_bus_4));
  OR12x8 OR12x8_1 (
    .Input_bus_22(Input_bus_11), .Input_bus_8(Input_bus_8), .Input_bus_6(Input_bus_9),
    .Input_bus_13(Input_bus_6), .Input_bus_4(Input_bus_1), .Input_bus_9(Input_bus_12),
    .Input_bus_19(Input_bus_2), .Input_bus_21(Input_bus_3), .Input_bus_5(Input_bus_4),
    .Input_bus_15(Input_bus_5), .Input_bus_3(Input_bus_7), .Input_bus_11(Input_bus_10),
    .Input_bus_24(DMX12x8_1_output_bus_6), .Input_bus_2(DMX12x8_1_output_bus_9),
    .Input_bus_1(DMX12x8_1_output_bus_5), .Input_bus_7(DMX12x8_1_output_bus_8),
    .Input_bus_17(DMX12x8_1_output_bus_12), .Input_bus_14(DMX12x8_1_output_bus_1),
    .Input_bus_20(DMX12x8_1_output_bus_11), .Input_bus_16(DMX12x8_1_output_bus_7),
    .Input_bus_10(DMX12x8_1_output_bus_10), .Input_bus_23(DMX12x8_1_output_bus_2),
    .Input_bus_12(DMX12x8_1_output_bus_3), .Input_bus_18(DMX12x8_1_output_bus_4),
    .Output_bus_5(Output_bus_1), .Output_bus_1(Output_bus_3), .Output_bus_8(Output_bus_2),
    .Output_bus_12(Output_bus_5), .Output_bus_3(Output_bus_10), .Output_bus_4(Output_bus_7),
    .Output_bus_9(Output_bus_4), .Output_bus_6(Output_bus_9), .Output_bus_7(Output_bus_11),
    .Output_bus_11(Output_bus_8), .Output_bus_10(Output_bus_6), .Output_bus_2(Output_bus_12));
endmodule

module Comp12bit (
  input  [11:0] in_1,
  input  [11:0] in_2,
  output out_3
);

  wire [11:0] xor_1_out;

  assign xor_1_out = in_1 ^ in_2;  // XOR_Gate xor_1, 12 bits wide
  nor nor_1 (out_3, xor_1_out[0], xor_1_out[1], xor_1_out[2], xor_1_out[3], xor_1_out[4], xor_1_out[5], xor_1_out[6], xor_1_out[7], xor_1_out[8], xor_1_out[9], xor_1_out[10], xor_1_out[11]);
endmodule

module GTEQ12 (
  input  [3:0] in_1,
  output o0,
  output o1,
  output o2,
  output o3,
  output o4,
  output o5,
  output o6,
  output o7,
  output o8,
  output o9,
  output o10,
  output o11
);

  wire and_1_out, and_2_out, and_3_out, and_4_out, and_5_out, and_6_out, and_7_out, and_8_out, and_9_out,
       and_10_out, and_11_out, and_12_out;

  or or_1 (o1, in_1[0], in_1[1], in_1[2], in_1[3]);
  or or_2 (o2, in_1[1], in_1[2], in_1[3]);
  and and_1 (and_1_out, in_1[1], in_1[0]);
  or or_3 (o3, and_1_out, in_1[2], in_1[3]);
  or or_4 (o4, in_1[2], in_1[3]);
  and and_2 (and_2_out, in_1[2], in_1[0]);
  or or_5 (o5, and_2_out, and_3_out, in_1[3]);
  and and_3 (and_3_out, in_1[2], in_1[1]);
  and and_4 (and_4_out, in_1[2], in_1[1]);
  or or_6 (o6, and_4_out, in_1[3]);
  and and_5 (and_5_out, in_1[2], in_1[1], in_1[0]);
  or or_7 (o7, and_5_out, in_1[3]);
  and and_6 (and_6_out, in_1[3], in_1[0]);
  or or_8 (o9, and_6_out, and_7_out, and_8_out);
  and and_7 (and_7_out, in_1[3], in_1[1]);
  and and_8 (and_8_out, in_1[3], in_1[2]);
  and and_9 (and_9_out, in_1[3], in_1[1]);
  or or_9 (o10, and_9_out, and_10_out);
  and and_10 (and_10_out, in_1[3], in_1[2]);
  and and_11 (and_11_out, in_1[3], in_1[1], in_1[0]);
  or or_10 (o11, and_11_out, and_12_out);
  and and_12 (and_12_out, in_1[3], in_1[2]);

  assign o0 = 1'b1;
  assign o8 = in_1[3];
endmodule

module mux12helper (
  input  [3:0] Input_bus_1,
  output o0,
  output o1,
  output o2,
  output o3,
  output o4,
  output o5,
  output o6,
  output o7,
  output o8,
  output o9,
  output o10,
  output o11
);

  wire not_1_out, not_2_out, not_3_out, not_4_out, not_5_out, not_6_out, not_7_out, not_8_out, not_9_out,
       not_10_out, not_11_out, not_12_out, not_13_out, not_14_out, not_15_out, not_16_out, not_17_out,
       not_18_out, not_19_out, not_20_out, not_21_out, not_22_out, not_23_out, not_24_out, not_25_out,
       not_26_out, not_27_out, not_28_out;

  not not_1 (not_1_out, Input_bus_1[3]);
  not not_2 (not_2_out, Input_bus_1[2]);
  not not_3 (not_3_out, Input_bus_1[1]);
  not not_4 (not_4_out, Input_bus_1[0]);
  not not_5 (not_5_out, Input_bus_1[3]);
  not not_6 (not_6_out, Input_bus_1[2]);
  not not_7 (not_7_out, Input_bus_1[1]);
  not not_8 (not_8_out, Input_bus_1[3]);
  not not_9 (not_9_out, Input_bus_1[2]);
  not not_10 (not_10_out, Input_bus_1[0]);
  not not_11 (not_11_out, Input_bus_1[3]);
  not not_12 (not_12_out, Input_bus_1[2]);
  not not_13 (not_13_out, Input_bus_1[3]);
  not not_14 (not_14_out, Input_bus_1[1]);
  not not_15 (not_15_out, Input_bus_1[0]);
  not not_16 (not_16_out, Input_bus_1[3]);
  not not_17 (not_17_out, Input_bus_1[1]);
  not not_18 (not_18_out, Input_bus_1[3]);
  not not_19 (not_19_out, Input_bus_1[0]);
  not not_20 (not_20_out, Input_bus_1[3]);
  not not_21 (not_21_out, Input_bus_1[2]);
  not not_22 (not_22_out, Input_bus_1[1]);
  not not_23 (not_23_out, Input_bus_1[0]);
  not not_24 (not_24_out, Input_bus_1[2]);
  not not_25 (not_25_out, Input_bus_1[1]);
  not not_26 (not_26_out, Input_bus_1[2]);
  not not_27 (not_27_out, Input_bus_1[0]);
  not not_28 (not_28_out, Input_bus_1[2]);
  and and_1 (o0, not_1_out, not_2_out, not_3_out, not_4_out);
  and and_2 (o1, not_5_out, not_6_out, not_7_out, Input_bus_1[0]);
  and and_3 (o2, not_8_out, not_9_out, Input_bus_1[1], not_10_out);
  and and_4 (o3, not_11_out, not_12_out, Input_bus_1[1], Input_bus_1[0]);
  and and_5 (o4, not_13_out, Input_bus_1[2], not_14_out, not_15_out);
  and and_6 (o5, not_16_out, Input_bus_1[2], not_17_out, Input_bus_1[0]);
  and and_7 (o6, not_18_out, Input_bus_1[2], Input_bus_1[1], not_19_out);
  and and_8 (o7, not_20_out, Input_bus_1[2], Input_bus_1[1], Input_bus_1[0]);
  and and_9 (o8, Input_bus_1[3], not_21_out, not_22_out, not_23_out);
  and and_10 (o9, Input_bus_1[3], not_24_out, not_25_out, Input_bus_1[0]);
  and and_11 (o10, Input_bus_1[3], not_26_out, Input_bus_1[1], not_27_out);
  and and_12 (o11, Input_bus_1[3], not_28_out, Input_bus_1[1], Input_bus_1[0]);
endmodule

module MUX12x8 (
  input  [7:0] Input_bus_3,
  input  [7:0] Input_bus_10,
  input  [7:0] Input_bus_8,
  input  [7:0] Input_bus_11,
  input  [7:0] Input_bus_2,
  input  [7:0] Input_bus_12,
  input  [7:0] Input_bus_4,
  input  [7:0] Input_bus_7,
  input  [7:0] Input_bus_5,
  input  [7:0] Input_bus_6,
  input  [7:0] Input_bus_9,
  input  [7:0] Input_bus_13,
  input  [3:0] Input_bus_1,
  output [7:0] Output_bus_1
);

  wire mux12helper_1_o0, mux12helper_1_o1, mux12helper_1_o2, mux12helper_1_o3, mux12helper_1_o4,
       mux12helper_1_o5, mux12helper_1_o6, mux12helper_1_o7, mux12helper_1_o8, mux12helper_1_o9,
       mux12helper_1_o10, mux12helper_1_o11;
  wire [7:0] Mask8bit_1_output_bus_1, Mask8bit_2_output_bus_1, Mask8bit_3_output_bus_1,
       Mask8bit_4_output_bus_1, Mask8bit_5_output_bus_1, Mask8bit_6_output_bus_1, Mask8bit_7_output_bus_1,
       Mask8bit_8_output_bus_1, Mask8bit_9_output_bus_1, Mask8bit_10_output_bus_1, Mask8bit_11_output_bus_1,
       Mask8bit_12_output_bus_1;

  Mask8bit Mask8bit_2 (.Input_bus_1(Input_bus_3), .Input_1(mux12helper_1_o0), .Output_bus_1(Mask8bit_2_output_bus_1));
  mux12helper mux12helper_1 (
    .Input_bus_1(Input_bus_1), .o0(mux12helper_1_o0), .o1(mux12helper_1_o1), .o2(mux12helper_1_o2),
    .o3(mux12helper_1_o3), .o4(mux12helper_1_o4), .o5(mux12helper_1_o5), .o6(mux12helper_1_o6),
    .o7(mux12helper_1_o7), .o8(mux12helper_1_o8), .o9(mux12helper_1_o9), .o10(mux12helper_1_o10),
    .o11(mux12helper_1_o11));
  Mask8bit Mask8bit_3 (.Input_bus_1(Input_bus_10), .Input_1(mux12helper_1_o1), .Output_bus_1(Mask8bit_3_output_bus_1));
  Mask8bit Mask8bit_5 (.Input_bus_1(Input_bus_8), .Input_1(mux12helper_1_o2), .Output_bus_1(Mask8bit_5_output_bus_1));
  Mask8bit Mask8bit_1 (.Input_bus_1(Input_bus_11), .Input_1(mux12helper_1_o3), .Output_bus_1(Mask8bit_1_output_bus_1));
  Mask8bit Mask8bit_6 (.Input_bus_1(Input_bus_2), .Input_1(mux12helper_1_o4), .Output_bus_1(Mask8bit_6_output_bus_1));
  Mask8bit Mask8bit_7 (.Input_bus_1(Input_bus_12), .Input_1(mux12helper_1_o5), .Output_bus_1(Mask8bit_7_output_bus_1));
  Mask8bit Mask8bit_4 (.Input_bus_1(Input_bus_4), .Input_1(mux12helper_1_o6), .Output_bus_1(Mask8bit_4_output_bus_1));
  Mask8bit Mask8bit_8 (.Input_bus_1(Input_bus_7), .Input_1(mux12helper_1_o7), .Output_bus_1(Mask8bit_8_output_bus_1));
  Mask8bit Mask8bit_12 (.Input_bus_1(Input_bus_5), .Input_1(mux12helper_1_o8), .Output_bus_1(Mask8bit_12_output_bus_1));
  Mask8bit Mask8bit_11 (.Input_bus_1(Input_bus_6), .Input_1(mux12helper_1_o9), .Output_bus_1(Mask8bit_11_output_bus_1));
  Mask8bit Mask8bit_10 (
    .Input_bus_1(Input_bus_9), .Input_1(mux12helper_1_o10), .Output_bus_1(Mask8bit_10_output_bus_1));
  Mask8bit Mask8bit_9 (.Input_bus_1(Input_bus_13), .Input_1(mux12helper_1_o11), .Output_bus_1(Mask8bit_9_output_bus_1));
  assign Output_bus_1 = Mask8bit_2_output_bus_1 | Mask8bit_3_output_bus_1 | Mask8bit_5_output_bus_1 | Mask8bit_1_output_bus_1 | Mask8bit_6_output_bus_1 | Mask8bit_7_output_bus_1 | Mask8bit_4_output_bus_1 | Mask8bit_8_output_bus_1 | Mask8bit_12_output_bus_1 | Mask8bit_11_output_bus_1 | Mask8bit_10_output_bus_1 | Mask8bit_9_output_bus_1;  // OR_Gate or_1, 8 bits wide
endmodule

module Mask8bit (
  input  [7:0] Input_bus_1,
  input  Input_1,
  output [7:0] Output_bus_1
);

  assign Output_bus_1 = Input_bus_1 & {8{Input_1}};  // AND_Gate and_1, 8 bits wide
endmodule

module DMX12x8 (
  input  [7:0] Input_bus_1,
  input  [3:0] Input_bus_2,
  output [7:0] Output_bus_6,
  output [7:0] Output_bus_9,
  output [7:0] Output_bus_5,
  output [7:0] Output_bus_8,
  output [7:0] Output_bus_12,
  output [7:0] Output_bus_1,
  output [7:0] Output_bus_11,
  output [7:0] Output_bus_7,
  output [7:0] Output_bus_10,
  output [7:0] Output_bus_2,
  output [7:0] Output_bus_3,
  output [7:0] Output_bus_4
);

  wire mux12helper_1_o0, mux12helper_1_o1, mux12helper_1_o2, mux12helper_1_o3, mux12helper_1_o4,
       mux12helper_1_o5, mux12helper_1_o6, mux12helper_1_o7, mux12helper_1_o8, mux12helper_1_o9,
       mux12helper_1_o10, mux12helper_1_o11;

  Mask8bit Mask8bit_4 (.Input_bus_1(Input_bus_1), .Input_1(mux12helper_1_o0), .Output_bus_1(Output_bus_6));
  mux12helper mux12helper_1 (
    .Input_bus_1(Input_bus_2), .o0(mux12helper_1_o0), .o1(mux12helper_1_o1), .o2(mux12helper_1_o2),
    .o3(mux12helper_1_o3), .o4(mux12helper_1_o4), .o5(mux12helper_1_o5), .o6(mux12helper_1_o6),
    .o7(mux12helper_1_o7), .o8(mux12helper_1_o8), .o9(mux12helper_1_o9), .o10(mux12helper_1_o10),
    .o11(mux12helper_1_o11));
  Mask8bit Mask8bit_6 (.Input_bus_1(Input_bus_1), .Input_1(mux12helper_1_o1), .Output_bus_1(Output_bus_9));
  Mask8bit Mask8bit_11 (.Input_bus_1(Input_bus_1), .Input_1(mux12helper_1_o2), .Output_bus_1(Output_bus_5));
  Mask8bit Mask8bit_7 (.Input_bus_1(Input_bus_1), .Input_1(mux12helper_1_o3), .Output_bus_1(Output_bus_8));
  Mask8bit Mask8bit_10 (.Input_bus_1(Input_bus_1), .Input_1(mux12helper_1_o4), .Output_bus_1(Output_bus_12));
  Mask8bit Mask8bit_5 (.Input_bus_1(Input_bus_1), .Input_1(mux12helper_1_o5), .Output_bus_1(Output_bus_1));
  Mask8bit Mask8bit_3 (.Input_bus_1(Input_bus_1), .Input_1(mux12helper_1_o6), .Output_bus_1(Output_bus_11));
  Mask8bit Mask8bit_1 (.Input_bus_1(Input_bus_1), .Input_1(mux12helper_1_o7), .Output_bus_1(Output_bus_7));
  Mask8bit Mask8bit_8 (.Input_bus_1(Input_bus_1), .Input_1(mux12helper_1_o8), .Output_bus_1(Output_bus_10));
  Mask8bit Mask8bit_9 (.Input_bus_1(Input_bus_1), .Input_1(mux12helper_1_o9), .Output_bus_1(Output_bus_2));
  Mask8bit Mask8bit_12 (.Input_bus_1(Input_bus_1), .Input_1(mux12helper_1_o10), .Output_bus_1(Output_bus_3));
  Mask8bit Mask8bit_2 (.Input_bus_1(Input_bus_1), .Input_1(mux12helper_1_o11), .Output_bus_1(Output_bus_4));
endmodule

module Mask12x8 (
  input  [7:0] Input_bus_10,
  input  [7:0] Input_bus_13,
  input  [7:0] Input_bus_5,
  input  [7:0] Input_bus_6,
  input  [7:0] Input_bus_4,
  input  [7:0] Input_bus_1,
  input  [7:0] Input_bus_2,
  input  [7:0] Input_bus_7,
  input  [7:0] Input_bus_9,
  input  [7:0] Input_bus_8,
  input  [7:0] Input_bus_3,
  input  [7:0] Input_bus_11,
  input  [11:0] Input_bus_12,
  output [7:0] Output_bus_10,
  output [7:0] Output_bus_11,
  output [7:0] Output_bus_4,
  output [7:0] Output_bus_2,
  output [7:0] Output_bus_12,
  output [7:0] Output_bus_6,
  output [7:0] Output_bus_8,
  output [7:0] Output_bus_3,
  output [7:0] Output_bus_5,
  output [7:0] Output_bus_9,
  output [7:0] Output_bus_1,
  output [7:0] Output_bus_7
);

  Mask8bit Mask8bit_4 (.Input_bus_1(Input_bus_10), .Input_1(Input_bus_12[0]), .Output_bus_1(Output_bus_10));
  Mask8bit Mask8bit_7 (.Input_bus_1(Input_bus_13), .Input_1(Input_bus_12[1]), .Output_bus_1(Output_bus_11));
  Mask8bit Mask8bit_1 (.Input_bus_1(Input_bus_5), .Input_1(Input_bus_12[2]), .Output_bus_1(Output_bus_4));
  Mask8bit Mask8bit_5 (.Input_bus_1(Input_bus_6), .Input_1(Input_bus_12[3]), .Output_bus_1(Output_bus_2));
  Mask8bit Mask8bit_11 (.Input_bus_1(Input_bus_4), .Input_1(Input_bus_12[4]), .Output_bus_1(Output_bus_12));
  Mask8bit Mask8bit_3 (.Input_bus_1(Input_bus_1), .Input_1(Input_bus_12[5]), .Output_bus_1(Output_bus_6));
  Mask8bit Mask8bit_12 (.Input_bus_1(Input_bus_2), .Input_1(Input_bus_12[6]), .Output_bus_1(Output_bus_8));
  Mask8bit Mask8bit_9 (.Input_bus_1(Input_bus_7), .Input_1(Input_bus_12[7]), .Output_bus_1(Output_bus_3));
  Mask8bit Mask8bit_8 (.Input_bus_1(Input_bus_9), .Input_1(Input_bus_12[8]), .Output_bus_1(Output_bus_5));
  Mask8bit Mask8bit_2 (.Input_bus_1(Input_bus_8), .Input_1(Input_bus_12[9]), .Output_bus_1(Output_bus_9));
  Mask8bit Mask8bit_10 (.Input_bus_1(Input_bus_3), .Input_1(Input_bus_12[10]), .Output_bus_1(Output_bus_1));
  Mask8bit Mask8bit_6 (.Input_bus_1(Input_bus_11), .Input_1(Input_bus_12[11]), .Output_bus_1(Output_bus_7));
endmodule

module OR12x8 (
  input  [7:0] Input_bus_24,
  input  [7:0] Input_bus_2,
  input  [7:0] Input_bus_1,
  input  [7:0] Input_bus_7,
  input  [7:0] Input_bus_17,
  input  [7:0] Input_bus_14,
  input  [7:0] Input_bus_20,
  input  [7:0] Input_bus_16,
  input  [7:0] Input_bus_10,
  input  [7:0] Input_bus_23,
  input  [7:0] Input_bus_12,
  input  [7:0] Input_bus_18,
  input  [7:0] Input_bus_22,
  input  [7:0] Input_bus_8,
  input  [7:0] Input_bus_6,
  input  [7:0] Input_bus_13,
  input  [7:0] Input_bus_4,
  input  [7:0] Input_bus_9,
  input  [7:0] Input_bus_19,
  input  [7:0] Input_bus_21,
  input  [7:0] Input_bus_5,
  input  [7:0] Input_bus_15,
  input  [7:0] Input_bus_3,
  input  [7:0] Input_bus_11,
  output [7:0] Output_bus_5,
  output [7:0] Output_bus_1,
  output [7:0] Output_bus_8,
  output [7:0] Output_bus_12,
  output [7:0] Output_bus_3,
  output [7:0] Output_bus_4,
  output [7:0] Output_bus_9,
  output [7:0] Output_bus_6,
  output [7:0] Output_bus_7,
  output [7:0] Output_bus_11,
  output [7:0] Output_bus_10,
  output [7:0] Output_bus_2
);

  assign Output_bus_5 = Input_bus_24 | Input_bus_22;  // OR_Gate or_1, 8 bits wide
  assign Output_bus_1 = Input_bus_2 | Input_bus_8;  // OR_Gate or_2, 8 bits wide
  assign Output_bus_8 = Input_bus_1 | Input_bus_6;  // OR_Gate or_3, 8 bits wide
  assign Output_bus_12 = Input_bus_7 | Input_bus_13;  // OR_Gate or_4, 8 bits wide
  assign Output_bus_3 = Input_bus_17 | Input_bus_4;  // OR_Gate or_5, 8 bits wide
  assign Output_bus_4 = Input_bus_14 | Input_bus_9;  // OR_Gate or_6, 8 bits wide
  assign Output_bus_9 = Input_bus_20 | Input_bus_19;  // OR_Gate or_7, 8 bits wide
  assign Output_bus_6 = Input_bus_16 | Input_bus_21;  // OR_Gate or_8, 8 bits wide
  assign Output_bus_7 = Input_bus_10 | Input_bus_5;  // OR_Gate or_9, 8 bits wide
  assign Output_bus_11 = Input_bus_23 | Input_bus_15;  // OR_Gate or_10, 8 bits wide
  assign Output_bus_10 = Input_bus_12 | Input_bus_3;  // OR_Gate or_11, 8 bits wide
  assign Output_bus_2 = Input_bus_18 | Input_bus_11;  // OR_Gate or_12, 8 bits wide
endmodule

module MUX2x2 (
  input  [1:0] Input_bus_2,
  input  [1:0] Input_bus_1,
  input  Input_1,
  output [1:0] Output_bus_1
);

  wire [1:0] and_1_out, and_2_out, not_1_out;

  assign not_1_out = ~{2{Input_1}};  // NOT_Gate not_1, 2 bits wide
  assign and_1_out = not_1_out & Input_bus_2;  // AND_Gate and_1, 2 bits wide
  assign and_2_out = Input_bus_1 & {2{Input_1}};  // AND_Gate and_2, 2 bits wide
  assign Output_bus_1 = and_1_out | and_2_out;  // OR_Gate or_1, 2 bits wide
endmodule

module MUX4x2 (
  input  [1:0] Input_bus_4,
  input  [1:0] Input_bus_2,
  input  [1:0] Input_bus_5,
  input  [1:0] Input_bus_1,
  input  [1:0] Input_bus_3,
  output [1:0] Output_bus_1
);

  wire [1:0] and_1_out, and_2_out, and_3_out, and_4_out;
  wire [1:1] not_1_out, not_2_out, not_3_out, not_4_out;

  not not_1 (not_1_out[1], Input_bus_3[0]);
  not not_2 (not_2_out[1], Input_bus_3[1]);
  not not_3 (not_3_out[1], Input_bus_3[1]);
  not not_4 (not_4_out[1], Input_bus_3[0]);
  assign and_1_out = {2{not_1_out[1]}} & Input_bus_4 & {2{not_2_out[1]}};  // AND_Gate and_1, 2 bits wide
  assign and_2_out = {2{Input_bus_3[0]}} & Input_bus_2 & {2{not_3_out[1]}};  // AND_Gate and_2, 2 bits wide
  assign and_3_out = {2{not_4_out[1]}} & Input_bus_5 & {2{Input_bus_3[1]}};  // AND_Gate and_3, 2 bits wide
  assign and_4_out = {2{Input_bus_3[0]}} & Input_bus_1 & {2{Input_bus_3[1]}};  // AND_Gate and_4, 2 bits wide
  assign Output_bus_1 = and_1_out | and_2_out | and_3_out | and_4_out;  // OR_Gate or_1, 2 bits wide
endmodule

module Comp2 (
  input  [1:0] Input_bus_1,
  input  [1:0] Input_bus_2,
  output Output_1
);

  wire [1:0] xor_1_out;

  assign xor_1_out = Input_bus_1 ^ Input_bus_2;  // XOR_Gate xor_1, 2 bits wide
  nor nor_1 (Output_1, xor_1_out[0], xor_1_out[1]);
endmodule

module Inc2bit (
  input  [1:0] Input_bus_1,
  output [1:0] Output_bus_1
);

  wire Half_adder_2_c;

  Half_adder Half_adder_1 (.A(Input_bus_1[1]), .B(Half_adder_2_c), .Q(Output_bus_1[1]));  // open: C
  Half_adder Half_adder_2 (.A(Input_bus_1[0]), .B(1'b1), .Q(Output_bus_1[0]), .C(Half_adder_2_c));
endmodule

module Inc8bit (
  input  [7:0] in_1,
  output [7:0] out_2
);

  wire half_adder_2_c, half_adder_3_c, half_adder_4_c, half_adder_5_c, half_adder_6_c, half_adder_7_c,
       half_adder_8_c;

  Half_adder half_adder_1 (.A(in_1[7]), .B(half_adder_2_c), .Q(out_2[7]));  // open: C
  Half_adder half_adder_2 (.A(in_1[6]), .B(half_adder_3_c), .Q(out_2[6]), .C(half_adder_2_c));
  Half_adder half_adder_3 (.A(in_1[5]), .B(half_adder_4_c), .Q(out_2[5]), .C(half_adder_3_c));
  Half_adder half_adder_4 (.A(in_1[4]), .B(half_adder_5_c), .Q(out_2[4]), .C(half_adder_4_c));
  Half_adder half_adder_5 (.A(in_1[3]), .B(half_adder_6_c), .Q(out_2[3]), .C(half_adder_5_c));
  Half_adder half_adder_6 (.A(in_1[2]), .B(half_adder_7_c), .Q(out_2[2]), .C(half_adder_6_c));
  Half_adder half_adder_7 (.A(in_1[1]), .B(half_adder_8_c), .Q(out_2[1]), .C(half_adder_7_c));
  Half_adder half_adder_8 (.A(in_1[0]), .B(1'b1), .Q(out_2[0]), .C(half_adder_8_c));
endmodule

module MUX4x4 (
  input  [3:0] Input_bus_1,
  input  [3:0] Input_bus_2,
  input  [3:0] Input_bus_4,
  input  [3:0] Input_bus_5,
  input  [1:0] Input_bus_3,
  output [3:0] Output_bus_1
);

  wire [3:0] and_1_out, and_2_out, and_3_out, and_4_out;
  wire [3:3] not_1_out, not_2_out, not_3_out, not_4_out;

  not not_1 (not_1_out[3], Input_bus_3[0]);
  not not_2 (not_2_out[3], Input_bus_3[1]);
  not not_3 (not_3_out[3], Input_bus_3[1]);
  not not_4 (not_4_out[3], Input_bus_3[0]);
  assign and_1_out = {4{not_1_out[3]}} & Input_bus_1 & {4{not_2_out[3]}};  // AND_Gate and_1, 4 bits wide
  assign and_2_out = {4{Input_bus_3[0]}} & Input_bus_2 & {4{not_3_out[3]}};  // AND_Gate and_2, 4 bits wide
  assign and_3_out = {4{not_4_out[3]}} & Input_bus_4 & {4{Input_bus_3[1]}};  // AND_Gate and_3, 4 bits wide
  assign and_4_out = {4{Input_bus_3[0]}} & Input_bus_5 & {4{Input_bus_3[1]}};  // AND_Gate and_4, 4 bits wide
  assign Output_bus_1 = and_1_out | and_2_out | and_3_out | and_4_out;  // OR_Gate or_1, 4 bits wide
  MUX4x2 MUX4x2_1 ();  // open: Input_bus_4, Input_bus_2, Input_bus_5, Input_bus_1, Input_bus_3, Output_bus_1
endmodule

module MUX2x4 (
  input  [3:0] Input_bus_2,
  input  [3:0] Input_bus_1,
  input  Input_1,
  output [3:0] Output_bus_1
);

  wire [3:0] and_1_out, and_2_out, not_1_out;

  assign not_1_out = ~{4{Input_1}};  // NOT_Gate not_1, 4 bits wide
  assign and_1_out = not_1_out & Input_bus_2;  // AND_Gate and_1, 4 bits wide
  assign and_2_out = Input_bus_1 & {4{Input_1}};  // AND_Gate and_2, 4 bits wide
  assign Output_bus_1 = and_1_out | and_2_out;  // OR_Gate or_1, 4 bits wide
endmodule

module MUX2x8 (
  input  [7:0] Input_bus_2,
  input  [7:0] Input_bus_1,
  input  Input_1,
  output [7:0] Output_bus_1
);

  wire not_1_out;
  wire [7:0] Mask8bit_1_output_bus_1, Mask8bit_2_output_bus_1;

  Mask8bit Mask8bit_1 (.Input_bus_1(Input_bus_2), .Input_1(not_1_out), .Output_bus_1(Mask8bit_1_output_bus_1));
  Mask8bit Mask8bit_2 (.Input_bus_1(Input_bus_1), .Input_1(Input_1), .Output_bus_1(Mask8bit_2_output_bus_1));
  not not_1 (not_1_out, Input_1);
  assign Output_bus_1 = Mask8bit_1_output_bus_1 | Mask8bit_2_output_bus_1;  // OR_Gate or_1, 8 bits wide
endmodule

module MUX4x8 (
  input  [7:0] in_1,
  input  [7:0] in_2,
  input  [7:0] in_3,
  input  [7:0] in_4,
  input  [1:0] in_5,
  output [7:0] out_6
);

  wire and_1_out, and_2_out, and_3_out, and_4_out, not_1_out, not_2_out, not_3_out, not_4_out;
  wire [7:0] mask8bit_1_output_bus_1, mask8bit_2_output_bus_1, mask8bit_3_output_bus_1,
       mask8bit_4_output_bus_1;

  Mask8bit mask8bit_1 (.Input_bus_1(in_1), .Input_1(and_1_out), .Output_bus_1(mask8bit_1_output_bus_1));
  Mask8bit mask8bit_2 (.Input_bus_1(in_2), .Input_1(and_2_out), .Output_bus_1(mask8bit_2_output_bus_1));
  and and_1 (and_1_out, not_3_out, not_1_out);
  and and_2 (and_2_out, in_5[0], not_2_out);
  not not_1 (not_1_out, in_5[1]);
  not not_2 (not_2_out, in_5[1]);
  not not_3 (not_3_out, in_5[0]);
  Mask8bit mask8bit_3 (.Input_bus_1(in_3), .Input_1(and_4_out), .Output_bus_1(mask8bit_3_output_bus_1));
  Mask8bit mask8bit_4 (.Input_bus_1(in_4), .Input_1(and_3_out), .Output_bus_1(mask8bit_4_output_bus_1));
  and and_3 (and_3_out, in_5[0], in_5[1]);
  and and_4 (and_4_out, not_4_out, in_5[1]);
  not not_4 (not_4_out, in_5[0]);
  assign out_6 = mask8bit_1_output_bus_1 | mask8bit_2_output_bus_1 | mask8bit_3_output_bus_1 | mask8bit_4_output_bus_1;  // OR_Gate or_1, 8 bits wide
endmodule

module DMX4x1 (
  input  Input_1,
  input  [1:0] Input_bus_1,
  output Output_1,
  output Output_2,
  output Output_3,
  output Output_4
);

  wire not_1_out, not_2_out, not_3_out, not_4_out;

  not not_1 (not_1_out, Input_bus_1[0]);
  not not_2 (not_2_out, Input_bus_1[1]);
  not not_3 (not_3_out, Input_bus_1[1]);
  not not_4 (not_4_out, Input_bus_1[0]);
  and and_1 (Output_1, not_1_out, Input_1, not_2_out);
  and and_2 (Output_2, Input_bus_1[0], Input_1, not_3_out);
  and and_3 (Output_3, not_4_out, Input_1, Input_bus_1[1]);
  and and_4 (Output_4, Input_bus_1[0], Input_1, Input_bus_1[1]);
endmodule

module DMX8x1 (
  input  Input_1,
  input  [2:0] Input_bus_1,
  output Output_4,
  output Output_8,
  output Output_7,
  output Output_1,
  output Output_6,
  output Output_3,
  output Output_5,
  output Output_2
);

  wire and_1_out, and_2_out, not_1_out;

  and and_1 (and_1_out, Input_1, not_1_out);
  not not_1 (not_1_out, Input_bus_1[2]);
  and and_2 (and_2_out, Input_1, Input_bus_1[2]);
  DMX4x1 DMX4x1_2 (
    .Input_bus_1(Input_bus_1[1:0]), .Output_1(Output_4), .Output_2(Output_8), .Output_3(Output_7),
    .Output_4(Output_1), .Input_1(and_1_out));
  DMX4x1 DMX4x1_1 (
    .Input_bus_1(Input_bus_1[1:0]), .Output_1(Output_6), .Output_2(Output_3), .Output_3(Output_5),
    .Output_4(Output_2), .Input_1(and_2_out));
endmodule

module Inc3bit (
  input  [2:0] Input_bus_1,
  output [2:0] Output_bus_1
);

  wire Half_adder_2_c, Half_adder_3_c;

  Half_adder Half_adder_1 (.A(Input_bus_1[2]), .B(Half_adder_2_c), .Q(Output_bus_1[2]));  // open: C
  Half_adder Half_adder_2 (.A(Input_bus_1[1]), .B(Half_adder_3_c), .Q(Output_bus_1[1]), .C(Half_adder_2_c));
  Half_adder Half_adder_3 (.A(Input_bus_1[0]), .B(1'b1), .Q(Output_bus_1[0]), .C(Half_adder_3_c));
endmodule

module Comp3 (
  input  [2:0] Input_bus_2,
  input  [2:0] Input_bus_1,
  output Output_1
);

  wire [2:0] xor_1_out;

  assign xor_1_out = Input_bus_2 ^ Input_bus_1;  // XOR_Gate xor_1, 3 bits wide
  nor nor_1 (Output_1, xor_1_out[0], xor_1_out[1], xor_1_out[2]);
endmodule

module ClockDiv (
  input  Input_1,
  input  [1:0] Input_bus_1,
  output Output_1
);

  wire and_1_out, and_2_out, and_3_out, and_4_out, d_ff_1_q, d_ff_1_qn, d_ff_2_q, d_ff_2_qn, d_ff_3_q,
       d_ff_3_qn, d_ff_4_q, d_ff_4_qn, d_ff_5_q, d_ff_5_qn, d_ff_6_q, d_ff_6_qn, not_1_out, not_2_out,
       not_3_out, not_4_out;

  D_Flip_Flop d_ff_1 (.D(d_ff_1_qn), .clk(Input_1), .Q(d_ff_1_q), .Qn(d_ff_1_qn));  // open: preset, reset
  D_Flip_Flop d_ff_2 (.D(d_ff_2_qn), .clk(Input_1), .Q(d_ff_2_q), .Qn(d_ff_2_qn));  // open: preset, reset
  D_Flip_Flop d_ff_3 (.D(d_ff_3_qn), .clk(Input_1), .Q(d_ff_3_q), .Qn(d_ff_3_qn));  // open: preset, reset
  D_Flip_Flop d_ff_4 (.D(d_ff_4_qn), .clk(d_ff_2_q), .Q(d_ff_4_q), .Qn(d_ff_4_qn));  // open: preset, reset
  D_Flip_Flop d_ff_5 (.D(d_ff_5_qn), .clk(d_ff_3_q), .Q(d_ff_5_q), .Qn(d_ff_5_qn));  // open: preset, reset
  D_Flip_Flop d_ff_6 (.D(d_ff_6_qn), .clk(d_ff_5_q), .Q(d_ff_6_q), .Qn(d_ff_6_qn));  // open: preset, reset
  not not_1 (not_1_out, Input_bus_1[0]);
  not not_2 (not_2_out, Input_bus_1[1]);
  not not_3 (not_3_out, Input_bus_1[1]);
  not not_4 (not_4_out, Input_bus_1[0]);
  and and_1 (and_1_out, not_1_out, Input_1, not_2_out);
  and and_2 (and_2_out, Input_bus_1[0], d_ff_1_q, not_3_out);
  and and_3 (and_3_out, not_4_out, d_ff_4_q, Input_bus_1[1]);
  and and_4 (and_4_out, Input_bus_1[0], d_ff_6_q, Input_bus_1[1]);
  or or_1 (Output_1, and_1_out, and_2_out, and_3_out, and_4_out);

  // Notes on the sheet:
  //   Clock input
  //   N div power
  //   Divides the clock frequency by 2^n, where n is the 2bit input value
  //   Clock output
endmodule

module LED_Connector (
  input  [7:0] Input_bus_1,
  output Output_7,
  output Output_1,
  output Output_5,
  output Output_6,
  output Output_3,
  output Output_4,
  output Output_8,
  output Output_2
);


  assign Output_1 = Input_bus_1[6];
  assign Output_2 = Input_bus_1[0];
  assign Output_3 = Input_bus_1[3];
  assign Output_4 = Input_bus_1[2];
  assign Output_5 = Input_bus_1[5];
  assign Output_6 = Input_bus_1[4];
  assign Output_7 = Input_bus_1[7];
  assign Output_8 = Input_bus_1[1];
endmodule

module Comp4 (
  input  [3:0] Input_bus_2,
  input  [3:0] Input_bus_1,
  output Output_1
);

  wire [3:0] xor_1_out;

  assign xor_1_out = Input_bus_2 ^ Input_bus_1;  // XOR_Gate xor_1, 4 bits wide
  nor nor_1 (Output_1, xor_1_out[0], xor_1_out[1], xor_1_out[2], xor_1_out[3]);
endmodule

module Inc4bit (
  input  [3:0] Input_bus_1,
  output [3:0] Output_bus_1
);

  wire Half_adder_1_c, Half_adder_3_c, Half_adder_4_c;

  Half_adder Half_adder_2 (.A(Input_bus_1[3]), .B(Half_adder_1_c), .Q(Output_bus_1[3]));  // open: C
  Half_adder Half_adder_1 (.A(Input_bus_1[2]), .B(Half_adder_3_c), .Q(Output_bus_1[2]), .C(Half_adder_1_c));
  Half_adder Half_adder_3 (.A(Input_bus_1[1]), .B(Half_adder_4_c), .Q(Output_bus_1[1]), .C(Half_adder_3_c));
  Half_adder Half_adder_4 (.A(Input_bus_1[0]), .B(1'b1), .Q(Output_bus_1[0]), .C(Half_adder_4_c));
endmodule

module Line_Check (
  input  [7:0] Player,
  input  [7:0] Memory_Line,
  output right_blocked,
  output left_blocked
);

  wire [7:0] and_1_out, and_2_out;

  assign and_1_out = Player & {1'b1, Memory_Line[7:1]};  // AND_Gate and_1, 8 bits wide
  assign and_2_out = Player & {Memory_Line[6:0], 1'b1};  // AND_Gate and_2, 8 bits wide
  or or_1 (right_blocked, and_2_out[0], and_2_out[1], and_2_out[2], and_2_out[3], and_2_out[4], and_2_out[5], and_2_out[6], and_2_out[7]);
  or or_2 (left_blocked, and_1_out[0], and_1_out[1], and_1_out[2], and_1_out[3], and_1_out[4], and_1_out[5], and_1_out[6], and_1_out[7]);
endmodule

module hor_freedom (
  input  right_blocked,
  input  left_blocked,
  input  right_button,
  input  left_button,
  output right,
  output straight,
  output left
);

  wire and_2_out, and_3_out, not_1_out, not_2_out, not_3_out, not_4_out, not_5_out, xor_1_out;

  not not_1 (not_1_out, right_blocked);
  not not_2 (not_2_out, left_button);
  not not_3 (not_3_out, right_button);
  not not_4 (not_4_out, left_blocked);
  and and_1 (right, not_1_out, right_button, not_2_out);
  and and_2 (and_2_out, right_blocked, right_button);
  xor xor_1 (xor_1_out, right_button, left_button);
  not not_5 (not_5_out, xor_1_out);
  and and_3 (and_3_out, left_button, left_blocked);
  and and_4 (left, left_button, not_3_out, not_4_out);
  or or_1 (straight, and_2_out, not_5_out, and_3_out);
endmodule

module hor_movement (
  input  [7:0] data_line,
  input  right_button,
  input  left_button,
  input  dir_select,
  input  clock,
  input  reset,
  output [7:0] player
);

  wire Line_Check_1_left_blocked, Line_Check_1_right_blocked;
  wire [7:0] and_1_out, and_2_out, and_3_out, or_1_out, rand_generator_1_output;
  wire [7:7] hor_freedom_1_left, hor_freedom_1_right, hor_freedom_1_straight;

  Register register_1 (.D(rand_generator_1_output), .en(dir_select), .clk(clock), .Q(player), .clr(reset));
  Line_Check Line_Check_1 (
    .Player(player), .Memory_Line(data_line), .right_blocked(Line_Check_1_right_blocked),
    .left_blocked(Line_Check_1_left_blocked));
  rand_generator rand_generator_1 (.\input (or_1_out), .clock(clock), .\output (rand_generator_1_output));
  hor_freedom hor_freedom_1 (
    .right_blocked(Line_Check_1_right_blocked), .left_blocked(Line_Check_1_left_blocked),
    .right_button(right_button), .left_button(left_button), .right(hor_freedom_1_right[7]),
    .straight(hor_freedom_1_straight[7]), .left(hor_freedom_1_left[7]));
  assign and_1_out = {1'b0, player[7:1]} & {8{hor_freedom_1_right[7]}};  // AND_Gate and_1, 8 bits wide
  assign and_2_out = player & {8{hor_freedom_1_straight[7]}};  // AND_Gate and_2, 8 bits wide
  assign and_3_out = {player[6:0], 1'b0} & {8{hor_freedom_1_left[7]}};  // AND_Gate and_3, 8 bits wide
  assign or_1_out = and_1_out | and_2_out | and_3_out;  // OR_Gate or_1, 8 bits wide
endmodule

module rand_generator (
  input  [7:0] \input ,
  input  clock,
  output [7:0] \output 
);

  wire undriven;
  wire [2:0] random_1_out;
  wire [7:0] and_1_out, and_2_out, bin_onehot_1_output;
  wire [7:7] not_1_out, or_1_out;

  or or_1 (or_1_out[7], \input [0], \input [1], \input [2], \input [3], \input [4], \input [5], \input [6], \input [7]);
  assign and_1_out = \input  & {8{or_1_out[7]}};  // AND_Gate and_1, 8 bits wide
  not not_1 (not_1_out[7], or_1_out[7]);
  assign and_2_out = bin_onehot_1_output & {8{not_1_out[7]}};  // AND_Gate and_2, 8 bits wide
  assign \output  = and_1_out | and_2_out;  // OR_Gate or_2, 8 bits wide
  Random #(.width(3)) random_1 (.clr(undriven), .next(not_1_out[7]), .clk(clock), .out(random_1_out));
  bin_onehot bin_onehot_1 (.\input (random_1_out), .\output (bin_onehot_1_output));
endmodule

module bin_onehot (
  input  [2:0] \input ,
  output [7:0] \output 
);

  wire not_1_out, not_2_out, not_3_out, not_4_out, not_5_out, not_6_out, not_7_out, not_8_out, not_9_out,
       not_10_out, not_11_out, not_12_out;

  and and_1 (\output [7], \input [2], \input [1], \input [0]);
  not not_1 (not_1_out, \input [0]);
  not not_2 (not_2_out, \input [1]);
  not not_3 (not_3_out, \input [1]);
  not not_4 (not_4_out, \input [0]);
  not not_5 (not_5_out, \input [2]);
  not not_6 (not_6_out, \input [2]);
  not not_7 (not_7_out, \input [0]);
  not not_8 (not_8_out, \input [2]);
  not not_9 (not_9_out, \input [1]);
  not not_10 (not_10_out, \input [2]);
  not not_11 (not_11_out, \input [1]);
  not not_12 (not_12_out, \input [0]);
  and and_2 (\output [6], \input [2], \input [1], not_1_out);
  and and_3 (\output [5], \input [2], not_2_out, \input [0]);
  and and_4 (\output [4], \input [2], not_3_out, not_4_out);
  and and_5 (\output [3], not_5_out, \input [1], \input [0]);
  and and_6 (\output [2], not_6_out, \input [1], not_7_out);
  and and_7 (\output [1], not_8_out, not_9_out, \input [0]);
  and and_8 (\output [0], not_10_out, not_11_out, not_12_out);
endmodule

module check_down (
  input  [7:0] player,
  input  [7:0] next_line,
  output next_line_blocked
);

  wire [7:0] and_1_out;

  assign and_1_out = player & next_line;  // AND_Gate and_1, 8 bits wide
  or or_1 (next_line_blocked, and_1_out[0], and_1_out[1], and_1_out[2], and_1_out[3], and_1_out[4], and_1_out[5], and_1_out[6], and_1_out[7]);
endmodule

module player (
  input  [7:0] data_line,
  input  right_button,
  input  left_button,
  input  clock,
  input  reset,
  input  [3:0] nb_side,
  input  [2:0] current_state,
  output [7:0] player_out,
  output [2:0] next_state
);

  wire d_ff_1_q, or_1_out;
  wire [2:0] and_1_out, and_2_out;
  wire [2:2] comparator3_1_equal, comparator_1_equal;
  wire [3:0] counter_1_counter;

  or or_1 (or_1_out, d_ff_1_q, reset);
  comparator3 comparator3_1 (.A(current_state), .B(3'b010), .equal(comparator3_1_equal[2]));
  counter counter_1 (.clock(clock), .reset(or_1_out), .counter(counter_1_counter), .enable(comparator3_1_equal[2]));
  // Probe on counter_1_counter
  comparator comparator_1 (.counter(counter_1_counter), .comp_val(nb_side), .equal(comparator_1_equal[2]));
  hor_movement hor_movement_1 (
    .data_line(data_line), .right_button(right_button), .left_button(left_button), .clock(clock),
    .reset(reset), .player(player_out), .dir_select(comparator3_1_equal[2]));
  D_Flip_Flop d_ff_1 (.D(comparator_1_equal[2]), .clk(clock), .Q(d_ff_1_q), .reset(reset));  // open: Qn, preset
  assign and_1_out = {3{comparator3_1_equal[2]}} & 3'b010;  // AND_Gate and_1, 3 bits wide
  assign next_state = and_1_out | and_2_out;  // OR_Gate or_2, 3 bits wide
  assign and_2_out = 3'b011 & {3{comparator_1_equal[2]}};  // AND_Gate and_2, 3 bits wide
endmodule

module counter (
  input  enable,
  input  clock,
  input  reset,
  output [3:0] counter
);

  wire Adder_1_o, Adder_2_cout, Adder_2_o, Adder_3_cout, Adder_3_o, Adder_4_cout, Adder_4_o;

  Adder Adder_1 (.A(1'b0), .B(counter[3]), .Cin(Adder_2_cout), .O(Adder_1_o));  // open: Cout
  Adder Adder_2 (.A(1'b0), .B(counter[2]), .Cin(Adder_3_cout), .Cout(Adder_2_cout), .O(Adder_2_o));
  Adder Adder_3 (.A(1'b0), .B(counter[1]), .Cin(Adder_4_cout), .Cout(Adder_3_cout), .O(Adder_3_o));
  Adder Adder_4 (.A(1'b0), .B(counter[0]), .Cin(enable), .Cout(Adder_4_cout), .O(Adder_4_o));
  D_Flip_Flop d_ff_1 (.D(Adder_1_o), .clk(clock), .Q(counter[3]), .reset(reset));  // open: Qn, preset
  D_Flip_Flop d_ff_2 (.D(Adder_2_o), .clk(clock), .Q(counter[2]), .reset(reset));  // open: Qn, preset
  D_Flip_Flop d_ff_3 (.D(Adder_3_o), .clk(clock), .Q(counter[1]), .reset(reset));  // open: Qn, preset
  D_Flip_Flop d_ff_4 (.D(Adder_4_o), .clk(clock), .Q(counter[0]), .reset(reset));  // open: Qn, preset
endmodule

module Half_adder (
  input  A,
  input  B,
  output Q,
  output C
);

  xor xor_1 (Q, B, A);
  and and_1 (C, A, B);
endmodule

module Adder (
  input  A,
  input  B,
  input  Cin,
  output Cout,
  output O
);

  wire Half_adder_1_c, Half_adder_2_c, Half_adder_2_q;

  Half_adder Half_adder_2 (.A(A), .B(B), .Q(Half_adder_2_q), .C(Half_adder_2_c));
  Half_adder Half_adder_1 (.A(Half_adder_2_q), .B(Cin), .Q(O), .C(Half_adder_1_c));
  or or_1 (Cout, Half_adder_2_c, Half_adder_1_c);
endmodule

module comparator (
  input  [3:0] counter,
  input  [3:0] comp_val,
  output equal
);

  wire [3:0] not_1_out, xor_1_out;

  assign xor_1_out = counter ^ comp_val;  // XOR_Gate xor_1, 4 bits wide
  assign not_1_out = ~xor_1_out;  // NOT_Gate not_1, 4 bits wide
  and and_1 (equal, not_1_out[0], not_1_out[1], not_1_out[2], not_1_out[3]);
endmodule

// current_state
module block_set (
  input  [2:0] line_nbr,
  input  [1:0] current_state,
  output write,
  output player_reset,
  output [1:0] next_state
);

  wire and_1_out;
  wire [1:0] and_2_out, and_4_out, and_5_out, not_1_out, not_3_out, xor_1_out;
  wire [1:1] and_3_out, undriven;
  wire [2:0] not_2_out, xor_2_out;

  assign xor_1_out = current_state ^ 2'b01;  // XOR_Gate xor_1, 2 bits wide
  and and_1 (and_1_out, not_1_out[0], not_1_out[1]);
  assign not_1_out = ~xor_1_out;  // NOT_Gate not_1, 2 bits wide
  counter counter_1 (.enable(and_1_out));  // open: clock, reset, counter
  assign xor_2_out = line_nbr ^ 3'b000;  // XOR_Gate xor_2, 3 bits wide
  assign not_2_out = ~xor_2_out;  // NOT_Gate not_2, 3 bits wide
  assign and_2_out = 2'b11 & {2{and_3_out[1]}};  // AND_Gate and_2, 2 bits wide
  and and_3 (and_3_out[1], not_2_out[0], not_2_out[1], not_2_out[2]);
  assign and_4_out = 2'b01 & not_3_out;  // AND_Gate and_4, 2 bits wide
  assign not_3_out = ~{2{undriven[1]}};  // NOT_Gate not_3, 2 bits wide
  assign and_5_out = {2{undriven[1]}} & and_2_out;  // AND_Gate and_5, 2 bits wide
  assign next_state = and_4_out | and_5_out;  // OR_Gate or_1, 2 bits wide
endmodule

module comparator3 (
  input  [2:0] A,
  input  [2:0] B,
  output equal
);

  wire [2:0] not_1_out, xor_1_out;

  assign xor_1_out = A ^ B;  // XOR_Gate xor_1, 3 bits wide
  and and_1 (equal, not_1_out[0], not_1_out[1], not_1_out[2]);
  assign not_1_out = ~xor_1_out;  // NOT_Gate not_1, 3 bits wide
endmodule

module read_current_line (
  input  [2:0] current_state,
  input  clock,
  input  [7:0] data_in,
  input  reset,
  input  [3:0] line_in,
  output [2:0] next_state,
  output [7:0] data_out,
  output [3:0] line_out
);

  wire not_1_out;
  wire [2:0] and_3_out, and_4_out, and_5_out, not_2_out;
  wire [2:2] and_2_out, d_ff_1_q;
  wire [3:3] comparator3_1_equal;

  D_Flip_Flop d_ff_1 (.D(comparator3_1_equal[3]), .clk(clock), .Q(d_ff_1_q[2]), .reset(reset));  // open: Qn, preset
  comparator3 comparator3_1 (.A(current_state), .B(3'b001), .equal(comparator3_1_equal[3]));
  Register register_1 (.D(data_in), .en(comparator3_1_equal[3]), .clk(clock), .Q(data_out), .clr(reset));
  assign line_out = {4{comparator3_1_equal[3]}} & line_in;  // AND_Gate and_1, 4 bits wide
  and and_2 (and_2_out[2], comparator3_1_equal[3], not_1_out);
  not not_1 (not_1_out, d_ff_1_q[2]);
  assign and_3_out = 3'b001 & {3{and_2_out[2]}};  // AND_Gate and_3, 3 bits wide
  assign and_4_out = 3'b010 & {3{d_ff_1_q[2]}};  // AND_Gate and_4, 3 bits wide
  assign and_5_out = 3'b000 & not_2_out;  // AND_Gate and_5, 3 bits wide
  assign not_2_out = ~{3{d_ff_1_q[2]}};  // NOT_Gate not_2, 3 bits wide
  assign next_state = and_3_out | and_4_out | and_5_out;  // OR_Gate or_1, 3 bits wide
endmodule

module read_next_line (
  input  [2:0] current_state,
  input  clock,
  input  [7:0] data_in,
  input  reset,
  input  [3:0] line_in,
  output [2:0] next_state,
  output [7:0] data_out,
  output [3:0] line_out
);

  wire not_1_out;
  wire [2:0] and_3_out, and_4_out, and_5_out, not_2_out;
  wire [2:2] and_2_out, d_ff_1_q;
  wire [3:0] adder4_1_o;
  wire [3:3] comparator3_1_equal;

  comparator3 comparator3_1 (.A(current_state), .B(3'b011), .equal(comparator3_1_equal[3]));
  D_Flip_Flop d_ff_1 (.D(comparator3_1_equal[3]), .clk(clock), .Q(d_ff_1_q[2]), .reset(reset));  // open: Qn, preset
  Register register_1 (.D(data_in), .en(comparator3_1_equal[3]), .clk(clock), .Q(data_out), .clr(reset));
  adder4 adder4_1 (.A(4'b0001), .B(line_in), .O(adder4_1_o));
  not not_1 (not_1_out, d_ff_1_q[2]);
  assign line_out = {4{comparator3_1_equal[3]}} & adder4_1_o;  // AND_Gate and_1, 4 bits wide
  and and_2 (and_2_out[2], comparator3_1_equal[3], not_1_out);
  assign not_2_out = ~{3{d_ff_1_q[2]}};  // NOT_Gate not_2, 3 bits wide
  assign and_3_out = {3{and_2_out[2]}} & 3'b011;  // AND_Gate and_3, 3 bits wide
  assign and_4_out = {3{d_ff_1_q[2]}} & 3'b100;  // AND_Gate and_4, 3 bits wide
  assign next_state = and_3_out | and_4_out | and_5_out;  // OR_Gate or_1, 3 bits wide
  assign and_5_out = 3'b000 & not_2_out;  // AND_Gate and_5, 3 bits wide
endmodule

module line_counter (
  input  plusone,
  input  reset,
  output [3:0] line_nbr
);

  wire Half_adder_1_c, Half_adder_1_q, Half_adder_2_c, Half_adder_2_q, Half_adder_3_c, Half_adder_3_q,
       Half_adder_4_q;

  Half_adder Half_adder_4 (.A(line_nbr[3]), .B(Half_adder_2_c), .Q(Half_adder_4_q));  // open: C
  Half_adder Half_adder_2 (.A(line_nbr[2]), .B(Half_adder_3_c), .Q(Half_adder_2_q), .C(Half_adder_2_c));
  Half_adder Half_adder_3 (.A(line_nbr[1]), .B(Half_adder_1_c), .Q(Half_adder_3_q), .C(Half_adder_3_c));
  Half_adder Half_adder_1 (.A(line_nbr[0]), .B(1'b1), .Q(Half_adder_1_q), .C(Half_adder_1_c));
  D_Flip_Flop d_ff_1 (.D(Half_adder_4_q), .clk(plusone), .Q(line_nbr[3]), .reset(reset));  // open: Qn, preset
  D_Flip_Flop d_ff_2 (.D(Half_adder_2_q), .clk(plusone), .Q(line_nbr[2]), .reset(reset));  // open: Qn, preset
  D_Flip_Flop d_ff_3 (.D(Half_adder_3_q), .clk(plusone), .Q(line_nbr[1]), .reset(reset));  // open: Qn, preset
  D_Flip_Flop d_ff_4 (.D(Half_adder_1_q), .clk(plusone), .Q(line_nbr[0]), .reset(reset));  // open: Qn, preset
endmodule

module blocked (
  input  [7:0] player,
  input  [7:0] next_line,
  input  [3:0] line_nbr,
  input  [2:0] current_state,
  output [2:0] next_state
);

  wire comparator_1_equal, or_1_out, or_2_out;
  wire [2:0] and_3_out, and_4_out, not_1_out, or_3_out;
  wire [2:2] and_2_out, comparator3_1_equal;
  wire [7:0] and_1_out;

  assign and_1_out = player & next_line;  // AND_Gate and_1, 8 bits wide
  comparator comparator_1 (.counter(line_nbr), .comp_val(4'b1011), .equal(comparator_1_equal));
  comparator3 comparator3_1 (.A(current_state), .B(3'b100), .equal(comparator3_1_equal[2]));
  or or_1 (or_1_out, and_1_out[0], and_1_out[1], and_1_out[2], and_1_out[3], and_1_out[4], and_1_out[5], and_1_out[6], and_1_out[7]);
  or or_2 (or_2_out, or_1_out, comparator_1_equal);
  and and_2 (and_2_out[2], or_2_out, comparator3_1_equal[2]);
  assign and_3_out = {3{and_2_out[2]}} & 3'b110;  // AND_Gate and_3, 3 bits wide
  assign not_1_out = ~{3{and_2_out[2]}};  // NOT_Gate not_1, 3 bits wide
  assign and_4_out = not_1_out & 3'b101;  // AND_Gate and_4, 3 bits wide
  assign or_3_out = and_3_out | and_4_out;  // OR_Gate or_3, 3 bits wide
  assign next_state = or_3_out & {3{comparator3_1_equal[2]}};  // AND_Gate and_5, 3 bits wide
endmodule

module line_nbr_plus (
  input  reset,
  input  [2:0] current_state,
  output [3:0] line_nbr,
  output [2:0] next_state
);

  wire [2:2] comparator3_1_equal;

  comparator3 comparator3_1 (.A(current_state), .B(3'b101), .equal(comparator3_1_equal[2]));
  line_counter line_counter_1 (.plusone(comparator3_1_equal[2]), .line_nbr(line_nbr), .reset(reset));
  assign next_state = {3{comparator3_1_equal[2]}} & 3'b001;  // AND_Gate and_1, 3 bits wide
endmodule

module adder4 (
  input  [3:0] A,
  input  [3:0] B,
  output [3:0] O
);

  wire Adder_1_cout, Adder_3_cout, Adder_4_cout;

  Adder Adder_2 (.A(A[3]), .B(B[3]), .Cin(Adder_3_cout), .O(O[3]));  // open: Cout
  Adder Adder_3 (.A(A[2]), .B(B[2]), .Cin(Adder_1_cout), .Cout(Adder_3_cout), .O(O[2]));
  Adder Adder_1 (.A(A[1]), .B(B[1]), .Cin(Adder_4_cout), .Cout(Adder_1_cout), .O(O[1]));
  Adder Adder_4 (.A(A[0]), .B(B[0]), .Cin(1'b0), .Cout(Adder_4_cout), .O(O[0]));
endmodule

module set_next_state (
  input  [2:0] current_state3,
  input  reset,
  input  clock,
  input  [1:0] current_state2,
  output [2:0] next_state3,
  output [1:0] duplicate_state2,
  output reset_state,
  output active
);

  wire comparator3_1_equal;
  wire [1:0] not_1_out, xor_1_out;
  wire [1:1] comparator3_2_equal;
  wire [2:0] and_3_out, and_4_out;
  wire [2:2] and_2_out;

  comparator3 comparator3_1 (.A(current_state3), .B(3'b000), .equal(comparator3_1_equal));
  comparator3 comparator3_2 (.A(current_state3), .B(3'b110), .equal(comparator3_2_equal[1]));
  assign xor_1_out = current_state2 ^ 2'b00;  // XOR_Gate xor_1, 2 bits wide
  assign not_1_out = ~xor_1_out;  // NOT_Gate not_1, 2 bits wide
  and and_1 (active, not_1_out[0], not_1_out[1]);
  and and_2 (and_2_out[2], comparator3_1_equal, active);
  D_Flip_Flop d_ff_1 (.D(comparator3_2_equal[1]), .clk(clock), .Q(reset_state), .reset(reset));  // open: Qn, preset
  assign and_3_out = {3{comparator3_2_equal[1]}} & 3'b000;  // AND_Gate and_3, 3 bits wide
  assign and_4_out = 3'b001 & {3{and_2_out[2]}};  // AND_Gate and_4, 3 bits wide
  assign duplicate_state2 = {2{comparator3_2_equal[1]}} & 2'b01;  // AND_Gate and_5, 2 bits wide
  assign next_state3 = and_3_out | and_4_out;  // OR_Gate or_1, 3 bits wide
endmodule
module display_number (
  input  [3:0] High,
  input  [3:0] Low,
  output [7:0] Zero,
  output [7:0] One,
  output [7:0] Two,
  output [7:0] Three,
  output [7:0] Four
);

  wire and_1_out, and_2_out, and_3_out, and_4_out, and_5_out, and_6_out, and_7_out, and_8_out, and_9_out,
       and_10_out, and_11_out, and_12_out, and_13_out, and_14_out, and_15_out, and_16_out, and_17_out,
       and_18_out, and_19_out, and_20_out, and_21_out, and_22_out, and_23_out, and_24_out, and_25_out,
       and_26_out, and_27_out, and_28_out, and_29_out, and_30_out, and_31_out, and_32_out, and_33_out,
       and_34_out, and_35_out, and_36_out, and_37_out, and_38_out, and_39_out, and_40_out, and_41_out,
       and_42_out, and_43_out, and_44_out, and_45_out, and_46_out, and_47_out, and_48_out, and_49_out,
       and_50_out, and_51_out, and_52_out, not_1_out, not_2_out, not_3_out, not_4_out, not_5_out, not_6_out,
       not_7_out, not_8_out, not_9_out, not_10_out, not_11_out, not_12_out, not_13_out, not_14_out,
       not_15_out, not_16_out, not_17_out, not_18_out, not_19_out, not_20_out, not_21_out, not_22_out,
       not_23_out, not_24_out, not_25_out, not_26_out, not_27_out, not_28_out, not_29_out, not_30_out,
       not_31_out, not_32_out, not_33_out, not_34_out, not_35_out, not_36_out, not_37_out, not_38_out,
       not_39_out, not_40_out, not_41_out, not_42_out, not_43_out, not_44_out, not_45_out, not_46_out,
       not_47_out, not_48_out, not_49_out, not_50_out, not_51_out, not_52_out, not_53_out, not_54_out,
       not_55_out, not_56_out, not_57_out, not_58_out, not_59_out, not_60_out, not_61_out, not_62_out,
       not_63_out, not_64_out, not_65_out, not_66_out, not_67_out, not_68_out, not_69_out, not_70_out;

  not not_1 (not_1_out, High[0]);
  not not_2 (not_2_out, High[2]);
  not not_3 (not_3_out, High[0]);
  not not_4 (not_4_out, High[1]);
  not not_5 (not_5_out, High[0]);
  not not_6 (not_6_out, High[1]);
  not not_7 (not_7_out, High[0]);
  not not_8 (not_8_out, High[1]);
  not not_9 (not_9_out, High[0]);
  not not_10 (not_10_out, High[2]);
  not not_11 (not_11_out, High[1]);
  not not_12 (not_12_out, High[2]);
  not not_13 (not_13_out, High[1]);
  not not_14 (not_14_out, High[0]);
  not not_15 (not_15_out, High[2]);
  not not_16 (not_16_out, High[1]);
  not not_17 (not_17_out, High[0]);
  not not_18 (not_18_out, High[2]);
  not not_19 (not_19_out, High[0]);
  not not_20 (not_20_out, High[0]);
  not not_21 (not_21_out, High[2]);
  not not_22 (not_22_out, High[0]);
  not not_23 (not_23_out, High[2]);
  not not_24 (not_24_out, High[0]);
  not not_25 (not_25_out, High[2]);
  not not_26 (not_26_out, High[0]);
  not not_27 (not_27_out, High[1]);
  not not_28 (not_28_out, High[2]);
  not not_29 (not_29_out, High[0]);
  not not_30 (not_30_out, High[2]);
  not not_31 (not_31_out, High[0]);
  not not_32 (not_32_out, High[1]);
  or or_1 (Zero[6], not_1_out, High[1], High[2], High[3]);
  and and_1 (and_1_out, not_2_out, not_3_out);
  and and_2 (and_2_out, High[2], High[0]);
  and and_3 (and_3_out, not_4_out, not_5_out);
  and and_4 (and_4_out, High[2], not_6_out);
  and and_5 (and_5_out, High[2], not_7_out);
  not not_33 (not_33_out, High[2]);
  and and_6 (and_6_out, not_8_out, not_9_out);
  and and_7 (and_7_out, High[2], High[1], High[0]);
  not not_34 (not_34_out, High[0]);
  and and_8 (and_8_out, not_10_out, High[1]);
  and and_9 (and_9_out, High[2], not_11_out);
  and and_10 (and_10_out, not_12_out, High[1]);
  and and_11 (and_11_out, High[2], not_13_out);
  and and_12 (and_12_out, High[2], not_14_out);
  and and_13 (and_13_out, High[2], High[1], High[0]);
  and and_14 (and_14_out, not_18_out, not_19_out);
  and and_15 (and_15_out, High[1], not_20_out);
  not not_35 (not_35_out, High[1]);
  and and_16 (and_16_out, not_21_out, High[0]);
  and and_17 (and_17_out, High[2], not_22_out);
  and and_18 (and_18_out, High[0], High[1], High[2]);
  and and_19 (and_19_out, not_23_out, not_24_out);
  and and_20 (and_20_out, not_25_out, High[1]);
  and and_21 (and_21_out, High[1], not_26_out);
  and and_22 (and_22_out, High[2], not_27_out, High[0]);
  and and_23 (and_23_out, not_28_out, not_29_out);
  and and_24 (and_24_out, not_30_out, High[1]);
  and and_25 (and_25_out, High[1], not_31_out);
  and and_26 (and_26_out, High[2], not_32_out, High[0]);
  or or_2 (Zero[5], and_1_out, High[1], and_2_out, High[3]);
  or or_3 (One[6], and_3_out, and_4_out, and_5_out, High[3]);
  or or_4 (One[4], not_33_out, and_6_out, and_7_out);
  or or_5 (Two[6], not_34_out, and_8_out, and_9_out, High[3]);
  or or_6 (Two[5], and_10_out, and_11_out, and_12_out, High[3]);
  or or_7 (Two[4], not_15_out, not_16_out, not_17_out, and_13_out);
  or or_8 (Three[6], and_14_out, and_15_out);
  or or_9 (Three[4], not_35_out, and_16_out, and_17_out, and_18_out);
  or or_10 (Four[6], and_19_out, and_20_out, and_21_out, and_22_out, High[3]);
  or or_11 (Four[5], and_23_out, and_24_out, and_25_out, and_26_out, High[3]);
  not not_36 (not_36_out, Low[0]);
  not not_37 (not_37_out, Low[2]);
  and and_27 (and_27_out, not_37_out, not_38_out);
  not not_38 (not_38_out, Low[0]);
  and and_28 (and_28_out, Low[2], Low[0]);
  not not_39 (not_39_out, Low[1]);
  and and_29 (and_29_out, not_39_out, not_40_out);
  not not_40 (not_40_out, Low[0]);
  and and_30 (and_30_out, Low[2], not_41_out);
  not not_41 (not_41_out, Low[1]);
  and and_31 (and_31_out, Low[2], not_42_out);
  not not_42 (not_42_out, Low[0]);
  not not_43 (not_43_out, Low[2]);
  not not_44 (not_44_out, Low[1]);
  and and_32 (and_32_out, not_44_out, not_45_out);
  not not_45 (not_45_out, Low[0]);
  not not_46 (not_46_out, Low[0]);
  not not_47 (not_47_out, Low[2]);
  and and_33 (and_33_out, not_47_out, Low[1]);
  and and_34 (and_34_out, Low[2], not_48_out);
  not not_48 (not_48_out, Low[1]);
  not not_49 (not_49_out, Low[2]);
  and and_35 (and_35_out, not_49_out, Low[1]);
  and and_36 (and_36_out, Low[2], not_50_out);
  not not_50 (not_50_out, Low[1]);
  and and_37 (and_37_out, Low[2], not_51_out);
  not not_51 (not_51_out, Low[0]);
  not not_52 (not_52_out, Low[2]);
  not not_53 (not_53_out, Low[1]);
  not not_54 (not_54_out, Low[0]);
  and and_38 (and_38_out, Low[2], Low[1], Low[0]);
  not not_55 (not_55_out, Low[2]);
  and and_39 (and_39_out, not_55_out, not_56_out);
  not not_56 (not_56_out, Low[0]);
  and and_40 (and_40_out, Low[1], not_57_out);
  not not_57 (not_57_out, Low[0]);
  not not_58 (not_58_out, Low[1]);
  not not_59 (not_59_out, Low[2]);
  and and_41 (and_41_out, not_59_out, Low[0]);
  and and_42 (and_42_out, Low[2], not_60_out);
  not not_60 (not_60_out, Low[0]);
  and and_43 (and_43_out, Low[2], Low[1], Low[0]);
  not not_61 (not_61_out, Low[2]);
  and and_44 (and_44_out, not_61_out, not_62_out);
  not not_62 (not_62_out, Low[0]);
  not not_63 (not_63_out, Low[2]);
  and and_45 (and_45_out, not_63_out, Low[1]);
  and and_46 (and_46_out, Low[1], not_64_out);
  not not_64 (not_64_out, Low[0]);
  not not_65 (not_65_out, Low[1]);
  and and_47 (and_47_out, Low[2], not_65_out, Low[0]);
  not not_66 (not_66_out, Low[2]);
  and and_48 (and_48_out, not_66_out, not_67_out);
  not not_67 (not_67_out, Low[0]);
  not not_68 (not_68_out, Low[2]);
  and and_49 (and_49_out, not_68_out, Low[1]);
  and and_50 (and_50_out, Low[1], not_69_out);
  not not_69 (not_69_out, Low[0]);
  not not_70 (not_70_out, Low[1]);
  and and_51 (and_51_out, Low[2], not_70_out, Low[0]);
  or or_12 (Zero[2], not_36_out, Low[1], Low[2], Low[3]);
  or or_13 (Zero[1], and_27_out, Low[1], and_28_out, Low[3]);
  or or_14 (One[2], and_29_out, and_30_out, and_31_out, Low[3]);
  or or_15 (One[0], not_43_out, and_52_out, and_32_out);
  and and_52 (and_52_out, Low[2], Low[1], Low[0]);
  or or_16 (Two[2], not_46_out, and_33_out, and_34_out, Low[3]);
  or or_17 (Two[1], and_35_out, and_36_out, and_37_out, Low[3]);
  or or_18 (Two[0], not_52_out, not_53_out, not_54_out, and_38_out);
  or or_19 (Three[2], and_39_out, and_40_out);
  or or_20 (Three[0], not_58_out, and_41_out, and_42_out, and_43_out);
  or or_21 (Four[2], and_44_out, and_45_out, and_46_out, and_47_out, Low[3]);
  or or_22 (Four[1], and_48_out, and_49_out, and_50_out, and_51_out, Low[3]);
  // NOT_Gate not_71 is placed but not wired

  assign {Four[7], Four[4:3], Four[0]} = 4'b0101;
  assign {One[7], One[5], One[3], One[1]} = 4'b0000;
  assign {Three[7], Three[5], Three[3], Three[1]} = 4'b0000;
  assign {Two[7], Two[3]} = 2'b00;
  assign {Zero[7], Zero[4:3], Zero[0]} = 4'b0101;
endmodule

module MUX6x3 (
  input  [2:0] Input_bus_1,
  input  [2:0] Input_bus_4,
  input  [2:0] Input_bus_3,
  input  [2:0] Input_bus_5,
  input  [2:0] Input_bus_2,
  input  [2:0] Input_bus_6,
  input  [2:0] current_state,
  output [2:0] Output_bus_1
);

  wire helper6_1_o1, helper6_1_o2, helper6_1_o3, helper6_1_o4, helper6_1_o5, helper6_1_o6;
  wire [2:0] mask3bit_1_output_bus_1, mask3bit_2_output_bus_1, mask3bit_3_output_bus_1,
       mask3bit_4_output_bus_1, mask3bit_5_output_bus_1, mask3bit_6_output_bus_1;

  mask3bit mask3bit_4 (.Input_bus_1(Input_bus_1), .Input_1(helper6_1_o1), .Output_bus_1(mask3bit_4_output_bus_1));
  mask3bit mask3bit_2 (.Input_bus_1(Input_bus_4), .Input_1(helper6_1_o2), .Output_bus_1(mask3bit_2_output_bus_1));
  mask3bit mask3bit_3 (.Input_bus_1(Input_bus_3), .Input_1(helper6_1_o3), .Output_bus_1(mask3bit_3_output_bus_1));
  mask3bit mask3bit_1 (.Input_bus_1(Input_bus_5), .Input_1(helper6_1_o4), .Output_bus_1(mask3bit_1_output_bus_1));
  helper6 helper6_1 (
    .Input_bus_1(current_state), .O1(helper6_1_o1), .O2(helper6_1_o2), .O3(helper6_1_o3), .O4(helper6_1_o4),
    .O5(helper6_1_o5), .O6(helper6_1_o6));
  mask3bit mask3bit_6 (.Input_bus_1(Input_bus_2), .Input_1(helper6_1_o5), .Output_bus_1(mask3bit_6_output_bus_1));
  mask3bit mask3bit_5 (.Input_bus_1(Input_bus_6), .Input_1(helper6_1_o6), .Output_bus_1(mask3bit_5_output_bus_1));
  assign Output_bus_1 = mask3bit_4_output_bus_1 | mask3bit_2_output_bus_1 | mask3bit_3_output_bus_1 | mask3bit_1_output_bus_1 | mask3bit_6_output_bus_1 | mask3bit_5_output_bus_1;  // OR_Gate or_1, 3 bits wide
endmodule

module mask3bit (
  input  [2:0] Input_bus_1,
  input  Input_1,
  output [2:0] Output_bus_1
);

  assign Output_bus_1 = Input_bus_1 & {3{Input_1}};  // AND_Gate and_1, 3 bits wide
endmodule

module helper6 (
  input  [2:0] Input_bus_1,
  output O1,
  output O2,
  output O3,
  output O4,
  output O5,
  output O6
);

  wire and_6_out, not_1_out, not_2_out, not_3_out, not_4_out, not_5_out, not_6_out, not_7_out, not_8_out,
       not_9_out, not_10_out, or_1_out;

  not not_1 (not_1_out, Input_bus_1[2]);
  not not_2 (not_2_out, Input_bus_1[1]);
  not not_3 (not_3_out, Input_bus_1[2]);
  not not_4 (not_4_out, Input_bus_1[0]);
  not not_5 (not_5_out, Input_bus_1[2]);
  not not_6 (not_6_out, Input_bus_1[1]);
  not not_7 (not_7_out, Input_bus_1[0]);
  not not_8 (not_8_out, Input_bus_1[1]);
  not not_9 (not_9_out, Input_bus_1[0]);
  and and_1 (O1, not_1_out, not_2_out, Input_bus_1[0]);
  and and_2 (O2, not_3_out, Input_bus_1[1], not_4_out);
  and and_3 (O3, not_5_out, Input_bus_1[1], Input_bus_1[0]);
  and and_4 (O4, Input_bus_1[2], not_6_out, not_7_out);
  and and_5 (O5, Input_bus_1[2], not_8_out, Input_bus_1[0]);
  and and_6 (and_6_out, Input_bus_1[2], Input_bus_1[1], not_9_out);
  or or_1 (or_1_out, Input_bus_1[2], Input_bus_1[1], Input_bus_1[0]);
  not not_10 (not_10_out, or_1_out);
  or or_2 (O6, and_6_out, not_10_out);
endmodule

module LeftShift8 (
  input  [7:0] Input_bus_1,
  output [7:0] Output_bus_1
);


  assign Output_bus_1 = {Input_bus_1[6:0], 1'b0};
endmodule

module RightShift8 (
  input  [7:0] Input_bus_1,
  output [7:0] Output_bus_1
);


  assign Output_bus_1 = {1'b0, Input_bus_1[7:1]};
endmodule

module IsZero8 (
  input  [7:0] Input_bus_1,
  output Output_1
);

  wire or_1_out;

  or or_1 (or_1_out, Input_bus_1[7], Input_bus_1[6], Input_bus_1[5], Input_bus_1[4], Input_bus_1[3], Input_bus_1[2], Input_bus_1[1], Input_bus_1[0]);
  not not_1 (Output_1, or_1_out);
endmodule

module PlayerIsBlocked (
  input  [7:0] Input_bus_1,
  input  [7:0] Input_bus_2,
  output Output_1
);

  wire IsZero8_1_output_1;
  wire [7:0] and_1_out;

  assign and_1_out = Input_bus_1 & Input_bus_2;  // AND_Gate and_1, 8 bits wide
  not not_1 (Output_1, IsZero8_1_output_1);
  IsZero8 IsZero8_1 (.Input_bus_1(and_1_out), .Output_1(IsZero8_1_output_1));
endmodule
